// Logisim project BonusProjectBusLayout.circ as structural Verilog: 4 circuits, main circuit CPU
module CPU (
);

  wire alu_1_equal, and_1_out, and_2_out, clock_1_out, clock_2_out, clock_3_out, clock_4_out, clock_5_out,
       clock_6_out, clock_7_out, clock_8_out, clock_9_out, clock_10_out, clock_11_out, clock_12_out,
       clock_13_out, clock_14_out, clock_15_out, clock_16_out, clock_17_out, clock_18_out, clock_19_out,
       clock_20_out, clock_21_out, clock_22_out, clock_23_out, clock_24_out, clock_25_out, clock_26_out,
       clock_27_out, clock_28_out, clock_29_out, clock_30_out, clock_31_out, clock_32_out, clock_33_out,
       clock_34_out, clock_35_out, clock_36_out, clock_37_out, clock_38_out, clock_39_out, clock_40_out,
       clock_41_out, clock_42_out, clock_43_out, clock_44_out, clock_45_out, control_1_aluvmemselect,
       control_1_aluvspcselect, control_1_beq, control_1_bne, control_1_imm_sel, control_1_j_jal,
       control_1_jr_jalr, control_1_we_mem, control_1_we_regfile, not_1_out, or_1_out, or_2_out,
       register_7_q, register_8_q, register_9_q, register_10_q, register_11_q, register_12_q, register_13_q,
       register_14_q, register_15_q, register_16_q, register_17_q, register_18_q, register_19_q,
       register_20_q, register_22_q, register_23_q, register_24_q, register_27_q, register_28_q,
       register_36_q, register_37_q, register_38_q, register_39_q, undriven, undriven_2, undriven_3;
  wire [3:0] control_1_alu_operation, register_26_q, register_32_q;
  wire [4:0] control_1_rd_select, control_1_rs_select, control_1_rt_select, register_25_q, register_29_q,
       register_30_q, register_31_q, register_35_q;
  wire [15:0] bit_extender_3_out, control_1_imm, register_5_q, register_6_q, shifter_1_out;
  wire [23:0] bit_extender_6_out, register_42_q;
  wire [25:0] bit_extender_4_out, shifter_2_out;
  wire [31:0] adder_1_out, adder_2_out, alu_1_res, bit_extender_1_out, bit_extender_2_out,
       bit_extender_5_out, multiplexer_1_out, multiplexer_2_out, multiplexer_3_out, multiplexer_4_out,
       multiplexer_5_out, multiplexer_6_out, ProgramCounter_q, ram_1_dout, regfile_1_data_rs,
       regfile_1_data_rt, register_1_q, register_2_q, register_4_q, register_33_q, register_34_q,
       register_41_q, rom_1_data, shifter_3_out;

  Register #(.width(32)) register_1 (.D(adder_1_out), .en(1'b1), .clk(clock_1_out), .Q(register_1_q));  // open: clr
  Clock clock_1 (.out(clock_1_out));
  Register #(.width(32)) register_2 (.D(register_1_q), .en(1'b1), .clk(clock_2_out), .Q(register_2_q));  // open: clr
  Clock clock_2 (.out(clock_2_out));
  Register #(.width(32)) register_3 (.en(1'b1), .clk(clock_3_out));  // open: D, Q, clr
  Clock clock_3 (.out(clock_3_out));
  Shifter #(.width(16)) shifter_1 (.in(register_5_q), .\dist (4'b0010), .out(shifter_1_out));
  Adder #(.width(32)) adder_1 (.a(ProgramCounter_q), .b(32'h4), .out(adder_1_out));  // open: cin, cout
  assign bit_extender_1_out = {{16{shifter_1_out[15]}}, shifter_1_out};  // Bit_Extender bit_extender_1
  Multiplexer #(.width(32)) multiplexer_1 (
    .in0(adder_1_out), .in1(adder_2_out), .out(multiplexer_1_out), .sel(or_1_out));
  Adder #(.width(32)) adder_2 (.a(adder_1_out), .b(bit_extender_1_out), .out(adder_2_out));  // open: cin, cout
  assign bit_extender_2_out = {{6{shifter_2_out[25]}}, shifter_2_out};  // Bit_Extender bit_extender_2
  Shifter #(.width(26)) shifter_2 (.in(bit_extender_4_out), .\dist (5'b00010), .out(shifter_2_out));
  or or_1 (or_1_out, and_2_out, and_1_out);
  Multiplexer #(.width(32)) multiplexer_2 (
    .in0(bit_extender_2_out), .in1(regfile_1_data_rs), .out(multiplexer_2_out), .sel(register_7_q));
  and and_1 (and_1_out, alu_1_equal, register_10_q);
  Shifter #(.shift("lr"), .width(32)) shifter_3 (.in(ProgramCounter_q), .\dist (5'b00010), .out(shifter_3_out));
  Register #(.width(32)) ProgramCounter (
    .D(multiplexer_3_out), .en(1'b1), .clk(clock_4_out), .Q(ProgramCounter_q));  // open: clr
  Multiplexer #(.width(32)) multiplexer_3 (
    .in0(multiplexer_1_out), .in1(multiplexer_2_out), .out(multiplexer_3_out), .sel(or_2_out));
  Clock clock_4 (.out(clock_4_out));
  and and_2 (and_2_out, register_8_q, not_1_out);
  not not_1 (not_1_out, alu_1_equal);
  Bit_Extender #(.in_width(32)) bit_extender_3 (.in(shifter_3_out), .out(bit_extender_3_out));
  ROM #(.addrWidth(16), .dataWidth(32)) rom_1 (.addr(bit_extender_3_out), .data(rom_1_data));
  // Probe on rom_1_data
  Bit_Extender #(.in_width(32), .out_width(26)) bit_extender_4 (.in(rom_1_data), .out(bit_extender_4_out));
  Multiplexer #(.width(32)) multiplexer_4 (
    .in0(alu_1_res), .in1(ram_1_dout), .out(multiplexer_4_out), .sel(register_13_q));
  Register #(.width(32)) register_4 (
    .D(multiplexer_5_out), .en(1'b1), .clk(clock_5_out), .Q(register_4_q));  // open: clr
  Multiplexer #(.width(32)) multiplexer_5 (
    .in0(multiplexer_4_out), .in1(register_2_q), .out(multiplexer_5_out), .sel(register_18_q));
  Clock clock_5 (.out(clock_5_out));
  Control control_1 (
    .Instruction(rom_1_data), .imm(control_1_imm), .rd_select(control_1_rd_select),
    .rt_select(control_1_rt_select), .rs_select(control_1_rs_select),
    .ALU_operation(control_1_alu_operation), .imm_sel(control_1_imm_sel), .we_regfile(control_1_we_regfile),
    .we_mem(control_1_we_mem), .ALUvMEMselect(control_1_aluvmemselect),
    .ALUvsPCselect(control_1_aluvspcselect), .J_Jal(control_1_j_jal), .BEQ(control_1_beq),
    .BNE(control_1_bne), .Jr_Jalr(control_1_jr_jalr));
  Register #(.width(16)) register_5 (.D(register_6_q), .en(1'b1), .clk(clock_6_out), .Q(register_5_q));  // open: clr
  Clock clock_6 (.out(clock_6_out));
  Register #(.width(16)) register_6 (.D(control_1_imm), .en(1'b1), .clk(clock_7_out), .Q(register_6_q));  // open: clr
  Clock clock_7 (.out(clock_7_out));
  Register #(.width(1)) register_7 (
    .D(control_1_jr_jalr), .en(1'b1), .clk(clock_8_out), .Q(register_7_q));  // open: clr
  Clock clock_8 (.out(clock_8_out));
  Register #(.width(1)) register_8 (.D(register_11_q), .en(1'b1), .clk(clock_9_out), .Q(register_8_q));  // open: clr
  Clock clock_9 (.out(clock_9_out));
  Register #(.width(1)) register_9 (.D(undriven), .en(1'b1), .clk(clock_10_out), .Q(register_9_q));  // open: clr
  Clock clock_10 (.out(clock_10_out));
  Register #(.width(1)) register_10 (.D(register_12_q), .en(1'b1), .clk(clock_11_out), .Q(register_10_q));  // open: clr
  Clock clock_11 (.out(clock_11_out));
  Register #(.width(1)) register_11 (.D(control_1_bne), .en(1'b1), .clk(clock_12_out), .Q(register_11_q));  // open: clr
  Clock clock_12 (.out(clock_12_out));
  Register #(.width(1)) register_12 (.D(control_1_beq), .en(1'b1), .clk(clock_13_out), .Q(register_12_q));  // open: clr
  Clock clock_13 (.out(clock_13_out));
  or or_2 (or_2_out, register_7_q, control_1_j_jal);
  Register #(.width(1)) register_13 (.D(register_14_q), .en(1'b1), .clk(clock_14_out), .Q(register_13_q));  // open: clr
  Clock clock_14 (.out(clock_14_out));
  Register #(.width(1)) register_14 (
    .D(control_1_aluvmemselect), .en(1'b1), .clk(clock_15_out), .Q(register_14_q));  // open: clr
  Clock clock_15 (.out(clock_15_out));
  Register #(.width(1)) register_15 (.en(1'b1), .clk(clock_16_out), .Q(register_15_q));  // open: D, clr
  Clock clock_16 (.out(clock_16_out));
  Register #(.width(1)) register_16 (.D(undriven_2), .en(1'b1), .clk(clock_17_out), .Q(register_16_q));  // open: clr
  Clock clock_17 (.out(clock_17_out));
  Register #(.width(1)) register_17 (.D(register_15_q), .en(1'b1), .clk(clock_18_out), .Q(register_17_q));  // open: clr
  Clock clock_18 (.out(clock_18_out));
  Register #(.width(1)) register_18 (.D(register_20_q), .en(1'b1), .clk(clock_19_out), .Q(register_18_q));  // open: clr
  Clock clock_19 (.out(clock_19_out));
  Register #(.width(1)) register_19 (.D(register_17_q), .en(1'b1), .clk(clock_20_out), .Q(register_19_q));  // open: clr
  Clock clock_20 (.out(clock_20_out));
  Register #(.width(1)) register_20 (
    .D(control_1_aluvspcselect), .en(1'b1), .clk(clock_21_out), .Q(register_20_q));  // open: clr
  Clock clock_21 (.out(clock_21_out));
  Register #(.width(1)) register_21 (.D(register_19_q), .en(1'b1), .clk(clock_22_out));  // open: Q, clr
  Clock clock_22 (.out(clock_22_out));
  Register #(.width(1)) register_22 (
    .D(control_1_imm_sel), .en(1'b1), .clk(clock_23_out), .Q(register_22_q));  // open: clr
  Clock clock_23 (.out(clock_23_out));
  Register #(.width(1)) register_23 (
    .D(control_1_we_regfile), .en(1'b1), .clk(clock_24_out), .Q(register_23_q));  // open: clr
  Clock clock_24 (.out(clock_24_out));
  Multiplexer #(.width(32)) multiplexer_6 (
    .in0(regfile_1_data_rt), .in1(bit_extender_5_out), .out(multiplexer_6_out), .sel(register_22_q));
  assign bit_extender_5_out = {{16{register_6_q[15]}}, register_6_q};  // Bit_Extender bit_extender_5
  Register #(.width(1)) register_24 (.D(register_23_q), .en(1'b1), .clk(clock_25_out), .Q(register_24_q));  // open: clr
  Clock clock_25 (.out(clock_25_out));
  Register #(.width(5)) register_25 (
    .D(control_1_rd_select), .en(1'b1), .clk(clock_26_out), .Q(register_25_q));  // open: clr
  Clock clock_26 (.out(clock_26_out));
  Register #(.width(4)) register_26 (
    .D(control_1_alu_operation), .en(1'b1), .clk(clock_27_out), .Q(register_26_q));  // open: clr
  Clock clock_27 (.out(clock_27_out));
  Register #(.width(1)) register_27 (.D(register_36_q), .en(1'b1), .clk(clock_28_out), .Q(register_27_q));  // open: clr
  Clock clock_28 (.out(clock_28_out));
  Register #(.width(1)) register_28 (.D(register_24_q), .en(1'b1), .clk(clock_29_out), .Q(register_28_q));  // open: clr
  Clock clock_29 (.out(clock_29_out));
  Register #(.width(5)) register_29 (
    .D(control_1_rs_select), .en(1'b1), .clk(clock_30_out), .Q(register_29_q));  // open: clr
  Clock clock_30 (.out(clock_30_out));
  Register #(.width(5)) register_30 (.D(register_25_q), .en(1'b1), .clk(clock_31_out), .Q(register_30_q));  // open: clr
  Clock clock_31 (.out(clock_31_out));
  Register #(.width(5)) register_31 (
    .D(control_1_rt_select), .en(1'b1), .clk(clock_32_out), .Q(register_31_q));  // open: clr
  Clock clock_32 (.out(clock_32_out));
  Register #(.width(4)) register_32 (.D(register_26_q), .en(1'b1), .clk(clock_33_out), .Q(register_32_q));  // open: clr
  Clock clock_33 (.out(clock_33_out));
  Register #(.width(32)) register_33 (
    .D(regfile_1_data_rs), .en(1'b1), .clk(clock_34_out), .Q(register_33_q));  // open: clr
  Clock clock_34 (.out(clock_34_out));
  Register #(.width(32)) register_34 (
    .D(multiplexer_6_out), .en(1'b1), .clk(clock_35_out), .Q(register_34_q));  // open: clr
  Clock clock_35 (.out(clock_35_out));
  Register #(.width(5)) register_35 (.D(register_30_q), .en(1'b1), .clk(clock_36_out), .Q(register_35_q));  // open: clr
  Clock clock_36 (.out(clock_36_out));
  Register #(.width(1)) register_36 (.D(register_37_q), .en(1'b1), .clk(clock_37_out), .Q(register_36_q));  // open: clr
  Clock clock_37 (.out(clock_37_out));
  Register #(.width(1)) register_37 (.D(undriven_3), .en(1'b1), .clk(clock_38_out), .Q(register_37_q));  // open: clr
  Clock clock_38 (.out(clock_38_out));
  ALU alu_1 (.operation(register_32_q), .op1(register_33_q), .op2(register_34_q), .Res(alu_1_res), .equal(alu_1_equal));
  regfile regfile_1 (
    .w_e(register_28_q), .rs(register_29_q), .data_in(register_4_q), .rd(register_35_q), .rt(register_31_q),
    .data_rs(regfile_1_data_rs), .data_rt(regfile_1_data_rt));
  Register #(.width(1)) register_38 (
    .D(control_1_we_mem), .en(1'b1), .clk(clock_39_out), .Q(register_38_q));  // open: clr
  Clock clock_39 (.out(clock_39_out));
  Register #(.width(1)) register_39 (.D(register_38_q), .en(1'b1), .clk(clock_40_out), .Q(register_39_q));  // open: clr
  Clock clock_40 (.out(clock_40_out));
  Register #(.width(1)) register_40 (.en(1'b1), .clk(clock_41_out));  // open: D, Q, clr
  Clock clock_41 (.out(clock_41_out));
  Register #(.width(32)) register_41 (
    .D(regfile_1_data_rt), .en(1'b1), .clk(clock_42_out), .Q(register_41_q));  // open: clr
  Clock clock_42 (.out(clock_42_out));
  Bit_Extender #(.in_width(32), .out_width(24)) bit_extender_6 (.in(alu_1_res), .out(bit_extender_6_out));
  Register #(.width(24)) register_42 (.en(1'b1), .clk(clock_43_out), .Q(register_42_q));  // open: D, clr
  Clock clock_43 (.out(clock_43_out));
  Register #(.width(32)) register_43 (.en(1'b1), .clk(clock_44_out));  // open: D, Q, clr
  Clock clock_44 (.out(clock_44_out));
  RAM #(.addrWidth(24), .dataWidth(32), .enables("line")) ram_1 (
    .addr(bit_extender_6_out), .we(register_39_q), .clk(clock_45_out), .din(register_41_q), .dout(ram_1_dout));
  Clock clock_45 (.out(clock_45_out));

  // Notes on the sheet:
  //   offset: (word addressed)
  //   PC + 4
  //   label: for j, jal (word addressed)
  //   PC + 4 + Offset
  //   register: for jr, jalr (byte addressed)
  //   jr/jalr
  //   any j*
  //   immediate
  //   label to jump to
  //   rs-data
  //   contents of rom_1 (hex, n*v repeats v):
  //   20100064 0 0 2002020 0 0 0 c000010 20500000 0 0 1600fff5 0 0 2002000a 800000f 20080008 41042
  //   21cd0001 21ee0001 0 0 0 3e00008
  //   probe to help test the value in a wire
  //   ALU
  //   PC + 4
  //   MEM
  //   jal/jalr
  //   value from memory
  //   1 if two registers are ==
  //   value from ALU
endmodule

module regfile (
  input  w_e,
  input  [4:0] rs,
  input  [31:0] data_in,
  input  [4:0] rd,
  input  [4:0] rt,
  output [31:0] data_rs,
  output [31:0] data_rt
);

  wire clock_1_out, demultiplexer_1_out1, demultiplexer_1_out2, demultiplexer_1_out3, demultiplexer_1_out4,
       demultiplexer_1_out5, demultiplexer_1_out6, demultiplexer_1_out7, demultiplexer_1_out8,
       demultiplexer_1_out9, demultiplexer_1_out10, demultiplexer_1_out11, demultiplexer_1_out12,
       demultiplexer_1_out13, demultiplexer_1_out14, demultiplexer_1_out15, demultiplexer_1_out16,
       demultiplexer_1_out17, demultiplexer_1_out18, demultiplexer_1_out19, demultiplexer_1_out20,
       demultiplexer_1_out21, demultiplexer_1_out22, demultiplexer_1_out23, demultiplexer_1_out24,
       demultiplexer_1_out25, demultiplexer_1_out26, demultiplexer_1_out27, demultiplexer_1_out28,
       demultiplexer_1_out29, demultiplexer_1_out30, demultiplexer_1_out31;
  wire [31:0] a0_q, a1_q, a2_q, a3_q, at_q, demultiplexer_2_out1, demultiplexer_2_out2, demultiplexer_2_out3,
       demultiplexer_2_out4, demultiplexer_2_out5, demultiplexer_2_out6, demultiplexer_2_out7,
       demultiplexer_2_out8, demultiplexer_2_out9, demultiplexer_2_out10, demultiplexer_2_out11,
       demultiplexer_2_out12, demultiplexer_2_out13, demultiplexer_2_out14, demultiplexer_2_out15,
       demultiplexer_2_out16, demultiplexer_2_out17, demultiplexer_2_out18, demultiplexer_2_out19,
       demultiplexer_2_out20, demultiplexer_2_out21, demultiplexer_2_out22, demultiplexer_2_out23,
       demultiplexer_2_out24, demultiplexer_2_out25, demultiplexer_2_out26, demultiplexer_2_out27,
       demultiplexer_2_out28, demultiplexer_2_out29, demultiplexer_2_out30, demultiplexer_2_out31, gp_q,
       k0_q, k1_q, ra_q, s0_q, s1_q, s2_q, s3_q, s4_q, s5_q, s6_q, s7_q, s8_q, sp_q, t0_q, t1_q, t2_q, t3_q,
       t4_q, t5_q, t6_q, t7_q, t8_q, t9_q, v0_q, v1_q;

  Demultiplexer #(.select(5)) demultiplexer_1 (
    .out1(demultiplexer_1_out1), .out2(demultiplexer_1_out2), .out3(demultiplexer_1_out3),
    .out4(demultiplexer_1_out4), .out5(demultiplexer_1_out5), .out6(demultiplexer_1_out6),
    .out7(demultiplexer_1_out7), .out8(demultiplexer_1_out8), .out9(demultiplexer_1_out9),
    .out10(demultiplexer_1_out10), .out11(demultiplexer_1_out11), .out12(demultiplexer_1_out12),
    .out13(demultiplexer_1_out13), .out14(demultiplexer_1_out14), .out15(demultiplexer_1_out15),
    .out16(demultiplexer_1_out16), .out17(demultiplexer_1_out17), .out18(demultiplexer_1_out18),
    .out19(demultiplexer_1_out19), .out20(demultiplexer_1_out20), .out21(demultiplexer_1_out21),
    .out22(demultiplexer_1_out22), .out23(demultiplexer_1_out23), .out24(demultiplexer_1_out24),
    .out25(demultiplexer_1_out25), .out26(demultiplexer_1_out26), .out27(demultiplexer_1_out27),
    .out28(demultiplexer_1_out28), .out29(demultiplexer_1_out29), .out30(demultiplexer_1_out30),
    .out31(demultiplexer_1_out31), .in(w_e), .sel(rd));  // open: out0
  Demultiplexer #(.select(5), .width(32)) demultiplexer_2 (
    .out1(demultiplexer_2_out1), .out2(demultiplexer_2_out2), .out3(demultiplexer_2_out3),
    .out4(demultiplexer_2_out4), .out5(demultiplexer_2_out5), .out6(demultiplexer_2_out6),
    .out7(demultiplexer_2_out7), .out8(demultiplexer_2_out8), .out9(demultiplexer_2_out9),
    .out10(demultiplexer_2_out10), .out11(demultiplexer_2_out11), .out12(demultiplexer_2_out12),
    .out13(demultiplexer_2_out13), .out14(demultiplexer_2_out14), .out15(demultiplexer_2_out15),
    .out16(demultiplexer_2_out16), .out17(demultiplexer_2_out17), .out18(demultiplexer_2_out18),
    .out19(demultiplexer_2_out19), .out20(demultiplexer_2_out20), .out21(demultiplexer_2_out21),
    .out22(demultiplexer_2_out22), .out23(demultiplexer_2_out23), .out24(demultiplexer_2_out24),
    .out25(demultiplexer_2_out25), .out26(demultiplexer_2_out26), .out27(demultiplexer_2_out27),
    .out28(demultiplexer_2_out28), .out29(demultiplexer_2_out29), .out30(demultiplexer_2_out30),
    .out31(demultiplexer_2_out31), .in(data_in), .sel(rd));  // open: out0
  Clock clock_1 (.out(clock_1_out));
  Register #(.width(32)) at (
    .D(demultiplexer_2_out1), .en(demultiplexer_1_out1), .clk(clock_1_out), .Q(at_q));  // open: clr
  Register #(.width(32)) v0 (
    .D(demultiplexer_2_out2), .en(demultiplexer_1_out2), .clk(clock_1_out), .Q(v0_q));  // open: clr
  Register #(.width(32)) v1 (
    .D(demultiplexer_2_out3), .en(demultiplexer_1_out3), .clk(clock_1_out), .Q(v1_q));  // open: clr
  Register #(.width(32)) a0 (
    .D(demultiplexer_2_out4), .en(demultiplexer_1_out4), .clk(clock_1_out), .Q(a0_q));  // open: clr
  Register #(.width(32)) a1 (
    .D(demultiplexer_2_out5), .en(demultiplexer_1_out5), .clk(clock_1_out), .Q(a1_q));  // open: clr
  Register #(.width(32)) a2 (
    .D(demultiplexer_2_out6), .en(demultiplexer_1_out6), .clk(clock_1_out), .Q(a2_q));  // open: clr
  Register #(.width(32)) a3 (
    .D(demultiplexer_2_out7), .en(demultiplexer_1_out7), .clk(clock_1_out), .Q(a3_q));  // open: clr
  Register #(.width(32)) t0 (
    .D(demultiplexer_2_out8), .en(demultiplexer_1_out8), .clk(clock_1_out), .Q(t0_q));  // open: clr
  Register #(.width(32)) t1 (
    .D(demultiplexer_2_out9), .en(demultiplexer_1_out9), .clk(clock_1_out), .Q(t1_q));  // open: clr
  Register #(.width(32)) t2 (
    .D(demultiplexer_2_out10), .en(demultiplexer_1_out10), .clk(clock_1_out), .Q(t2_q));  // open: clr
  Register #(.width(32)) t3 (
    .D(demultiplexer_2_out11), .en(demultiplexer_1_out11), .clk(clock_1_out), .Q(t3_q));  // open: clr
  Register #(.width(32)) t4 (
    .D(demultiplexer_2_out12), .en(demultiplexer_1_out12), .clk(clock_1_out), .Q(t4_q));  // open: clr
  Register #(.width(32)) t5 (
    .D(demultiplexer_2_out13), .en(demultiplexer_1_out13), .clk(clock_1_out), .Q(t5_q));  // open: clr
  Register #(.width(32)) t6 (
    .D(demultiplexer_2_out14), .en(demultiplexer_1_out14), .clk(clock_1_out), .Q(t6_q));  // open: clr
  Register #(.width(32)) t7 (
    .D(demultiplexer_2_out15), .en(demultiplexer_1_out15), .clk(clock_1_out), .Q(t7_q));  // open: clr
  Register #(.width(32)) s0 (
    .D(demultiplexer_2_out16), .en(demultiplexer_1_out16), .clk(clock_1_out), .Q(s0_q));  // open: clr
  Register #(.width(32)) s1 (
    .D(demultiplexer_2_out17), .en(demultiplexer_1_out17), .clk(clock_1_out), .Q(s1_q));  // open: clr
  Register #(.width(32)) s2 (
    .D(demultiplexer_2_out18), .en(demultiplexer_1_out18), .clk(clock_1_out), .Q(s2_q));  // open: clr
  Register #(.width(32)) s3 (
    .D(demultiplexer_2_out19), .en(demultiplexer_1_out19), .clk(clock_1_out), .Q(s3_q));  // open: clr
  Register #(.width(32)) s4 (
    .D(demultiplexer_2_out20), .en(demultiplexer_1_out20), .clk(clock_1_out), .Q(s4_q));  // open: clr
  Register #(.width(32)) s5 (
    .D(demultiplexer_2_out21), .en(demultiplexer_1_out21), .clk(clock_1_out), .Q(s5_q));  // open: clr
  Register #(.width(32)) s6 (
    .D(demultiplexer_2_out22), .en(demultiplexer_1_out22), .clk(clock_1_out), .Q(s6_q));  // open: clr
  Register #(.width(32)) s7 (
    .D(demultiplexer_2_out23), .en(demultiplexer_1_out23), .clk(clock_1_out), .Q(s7_q));  // open: clr
  Register #(.width(32)) t8 (
    .D(demultiplexer_2_out24), .en(demultiplexer_1_out24), .clk(clock_1_out), .Q(t8_q));  // open: clr
  Register #(.width(32)) t9 (
    .D(demultiplexer_2_out25), .en(demultiplexer_1_out25), .clk(clock_1_out), .Q(t9_q));  // open: clr
  Register #(.width(32)) k0 (
    .D(demultiplexer_2_out26), .en(demultiplexer_1_out26), .clk(clock_1_out), .Q(k0_q));  // open: clr
  Register #(.width(32)) k1 (
    .D(demultiplexer_2_out27), .en(demultiplexer_1_out27), .clk(clock_1_out), .Q(k1_q));  // open: clr
  Register #(.width(32)) gp (
    .D(demultiplexer_2_out28), .en(demultiplexer_1_out28), .clk(clock_1_out), .Q(gp_q));  // open: clr
  Register #(.width(32)) sp (
    .D(demultiplexer_2_out29), .en(demultiplexer_1_out29), .clk(clock_1_out), .Q(sp_q));  // open: clr
  Register #(.width(32)) s8 (
    .D(demultiplexer_2_out30), .en(demultiplexer_1_out30), .clk(clock_1_out), .Q(s8_q));  // open: clr
  Register #(.width(32)) ra (
    .D(demultiplexer_2_out31), .en(demultiplexer_1_out31), .clk(clock_1_out), .Q(ra_q));  // open: clr
  Multiplexer #(.select(5), .width(32)) multiplexer_1 (
    .in0({32{1'b0}}), .in1(at_q), .in2(v0_q), .in3(v1_q), .in4(a0_q), .in5(a1_q), .in6(a2_q), .in7(a3_q),
    .in8(t0_q), .in9(t1_q), .in10(t2_q), .in11(t3_q), .in12(t4_q), .in13(t5_q), .in14(t6_q), .in15(t7_q),
    .in16(s0_q), .in17(s1_q), .in18(s2_q), .in19(s3_q), .in20(s4_q), .in21(s5_q), .in22(s6_q), .in23(s7_q),
    .in24(t8_q), .in25(t9_q), .in26(k0_q), .in27(k1_q), .in28(gp_q), .in29(sp_q), .in30(s8_q), .in31(ra_q),
    .out(data_rs), .sel(rs));
  Multiplexer #(.select(5), .width(32)) multiplexer_2 (
    .in0({32{1'b0}}), .in1(at_q), .in2(v0_q), .in3(v1_q), .in4(a0_q), .in5(a1_q), .in6(a2_q), .in7(a3_q),
    .in8(t0_q), .in9(t1_q), .in10(t2_q), .in11(t3_q), .in12(t4_q), .in13(t5_q), .in14(t6_q), .in15(t7_q),
    .in16(s0_q), .in17(s1_q), .in18(s2_q), .in19(s3_q), .in20(s4_q), .in21(s5_q), .in22(s6_q), .in23(s7_q),
    .in24(t8_q), .in25(t9_q), .in26(k0_q), .in27(k1_q), .in28(gp_q), .in29(sp_q), .in30(s8_q), .in31(ra_q),
    .out(data_rt), .sel(rt));
endmodule

module ALU (
  input  [3:0] operation,
  input  [31:0] op1,
  input  [31:0] op2,
  output [31:0] Res,
  output equal
);

  wire clock_1_out, comparator_1_lt;
  wire [4:0] bit_extender_1_out, bit_extender_2_out;
  wire [31:0] adder_1_out, bit_extender_3_out, divider_1_out, divider_1_rem, HI_q, LO_q, multiplexer_2_out,
       multiplexer_3_out, multiplier_1_cout, multiplier_1_out, shifter_1_out, shifter_2_out, subtractor_1_out;

  Adder #(.width(32)) adder_1 (.a(op1), .b(op2), .out(adder_1_out));  // open: cin, cout
  Subtractor #(.width(32)) subtractor_1 (.a(op1), .b(op2), .out(subtractor_1_out));  // open: bin, bout
  Multiplier #(.width(32)) multiplier_1 (
    .a(op1), .b(op2), .out(multiplier_1_out), .cout(multiplier_1_cout));  // open: cin
  Divider #(.width(32)) divider_1 (.a(op1), .b(op2), .out(divider_1_out), .rem(divider_1_rem));  // open: upper
  Shifter #(.shift("lr"), .width(32)) shifter_1 (.in(op1), .\dist (bit_extender_1_out), .out(shifter_1_out));
  Bit_Extender #(.in_width(32), .out_width(5), .\type ("zero")) bit_extender_1 (.in(op2), .out(bit_extender_1_out));
  Shifter #(.width(32)) shifter_2 (.in(op1), .\dist (bit_extender_2_out), .out(shifter_2_out));
  Bit_Extender #(.in_width(32), .out_width(5), .\type ("zero")) bit_extender_2 (.in(op2), .out(bit_extender_2_out));
  Comparator #(.width(32)) comparator_1 (.a(op1), .b(op2), .eq(equal), .lt(comparator_1_lt));  // open: gt
  assign bit_extender_3_out = {{31{1'b0}}, comparator_1_lt};  // Bit_Extender bit_extender_3
  Multiplexer #(.select(4), .width(32)) multiplexer_1 (
    .in0(adder_1_out), .in1(subtractor_1_out), .in2(multiplier_1_out), .in3(divider_1_out), .in4(LO_q),
    .in5(HI_q), .in6(shifter_1_out), .in7(shifter_2_out), .in8(bit_extender_3_out), .out(Res), .sel(operation));  // open: in9, in10, in11, in12, in13, in14, in15
  Multiplexer #(.select(4), .width(32)) multiplexer_2 (
    .in0(LO_q), .in1(LO_q), .in2(multiplier_1_out), .in3(divider_1_out), .in4(LO_q), .in5(LO_q), .in6(LO_q),
    .in7(LO_q), .in8(LO_q), .in9(LO_q), .in10(LO_q), .in11(LO_q), .in12(LO_q), .in13(LO_q), .in14(LO_q),
    .in15(LO_q), .out(multiplexer_2_out), .sel(operation));
  Multiplexer #(.select(4), .width(32)) multiplexer_3 (
    .in0(HI_q), .in1(HI_q), .in2(multiplier_1_cout), .in3(divider_1_rem), .in4(HI_q), .in5(HI_q), .in6(HI_q),
    .in7(HI_q), .in8(HI_q), .in9(HI_q), .in10(HI_q), .in11(HI_q), .in12(HI_q), .in13(HI_q), .in14(HI_q),
    .in15(HI_q), .out(multiplexer_3_out), .sel(operation));
  Register #(.width(32)) LO (.D(multiplexer_2_out), .clk(clock_1_out), .Q(LO_q));  // open: en, clr
  Register #(.width(32)) HI (.D(multiplexer_3_out), .clk(clock_1_out), .Q(HI_q));  // open: en, clr
  Clock clock_1 (.out(clock_1_out));
endmodule

module Control (
  input  [31:0] Instruction,
  output [15:0] imm,
  output [4:0] rd_select,
  output [4:0] rt_select,
  output [4:0] rs_select,
  output [3:0] ALU_operation,
  output imm_sel,
  output we_regfile,
  output we_mem,
  output ALUvMEMselect,
  output ALUvsPCselect,
  output J_Jal,
  output BEQ,
  output BNE,
  output Jr_Jalr
);

  wire and_1_out, and_2_out, and_3_out, and_4_out, and_5_out, and_6_out, and_7_out, and_8_out, and_9_out,
       and_10_out, and_11_out, and_12_out, and_13_out, and_18_out, and_19_out, and_20_out, and_22_out,
       comparator_1_eq, comparator_2_eq, nor_1_out, not_1_out, not_2_out, not_3_out, not_4_out, not_5_out,
       not_6_out, not_7_out, not_8_out, not_9_out, not_10_out, not_11_out, not_12_out, not_13_out,
       not_14_out, not_15_out, not_16_out, not_17_out, not_18_out, not_19_out, not_20_out, not_21_out,
       not_22_out, not_23_out, not_24_out, not_25_out, not_26_out, not_27_out, or_1_out, or_2_out, or_3_out,
       or_4_out, or_6_out, or_9_out;
  wire [3:0] adder_1_out, adder_2_out, adder_3_out, adder_4_out, adder_5_out, adder_6_out,
       bit_extender_3_out, bit_extender_4_out, bit_extender_5_out, bit_extender_6_out, bit_extender_7_out,
       bit_extender_8_out, bit_extender_9_out, bit_extender_10_out, multiplier_1_out, multiplier_2_out,
       multiplier_3_out, multiplier_4_out, multiplier_5_out, multiplier_6_out, multiplier_7_out,
       multiplier_8_out;
  wire [4:0] multiplexer_4_out;
  wire [15:0] bit_extender_1_out, bit_extender_2_out, multiplexer_1_out;

  not not_1 (not_1_out, comparator_1_eq);
  Comparator #(.width(32)) comparator_1 (.a(Instruction), .b({32{1'b0}}), .eq(comparator_1_eq));  // open: gt, lt
  Comparator #(.width(6)) comparator_2 (.a(Instruction[31:26]), .b({6{1'b0}}), .eq(comparator_2_eq));  // open: gt, lt
  Bit_Extender #(.in_width(26)) bit_extender_1 (.in(Instruction[25:0]), .out(bit_extender_1_out));
  assign bit_extender_2_out = {{11{1'b0}}, Instruction[10:6]};  // Bit_Extender bit_extender_2
  not not_2 (not_2_out, Instruction[1]);
  not not_3 (not_3_out, Instruction[3]);
  not not_4 (not_4_out, Instruction[1]);
  not not_5 (not_5_out, Instruction[3]);
  not not_6 (not_6_out, Instruction[3]);
  not not_7 (not_7_out, Instruction[1]);
  not not_8 (not_8_out, Instruction[5]);
  not not_9 (not_9_out, Instruction[4]);
  not not_10 (not_10_out, Instruction[4]);
  not not_11 (not_11_out, Instruction[3]);
  not not_12 (not_12_out, Instruction[5]);
  not not_13 (not_13_out, Instruction[1]);
  not not_14 (not_14_out, Instruction[31]);
  not not_15 (not_15_out, Instruction[5]);
  not not_16 (not_16_out, Instruction[4]);
  not not_17 (not_17_out, Instruction[2]);
  not not_18 (not_18_out, Instruction[0]);
  not not_19 (not_19_out, Instruction[29]);
  not not_20 (not_20_out, Instruction[26]);
  not not_21 (not_21_out, Instruction[31]);
  not not_22 (not_22_out, Instruction[26]);
  not not_23 (not_23_out, Instruction[31]);
  Multiplexer #(.width(16)) multiplexer_1 (
    .in0(Instruction[15:0]), .in1(bit_extender_2_out), .out(multiplexer_1_out), .sel(comparator_2_eq));
  and and_1 (and_1_out, not_2_out, Instruction[5], comparator_2_eq);
  and and_2 (and_2_out, Instruction[5], comparator_2_eq, not_3_out, Instruction[1]);
  and and_3 (and_3_out, comparator_2_eq, Instruction[4], Instruction[3], not_4_out);
  and and_4 (and_4_out, comparator_2_eq, Instruction[4], Instruction[3], Instruction[1]);
  and and_5 (and_5_out, comparator_2_eq, Instruction[4], not_5_out, Instruction[1]);
  and and_6 (and_6_out, comparator_2_eq, Instruction[4], not_6_out, not_7_out);
  and and_7 (and_7_out, comparator_2_eq, not_8_out, not_9_out, Instruction[1]);
  and and_8 (and_8_out, comparator_2_eq, not_10_out, not_11_out, not_12_out, not_13_out);
  and and_9 (and_9_out, comparator_2_eq, Instruction[5], Instruction[3], Instruction[1]);
  and and_10 (and_10_out, Instruction[29], not_14_out);
  and and_11 (and_11_out, comparator_2_eq, Instruction[0]);
  and and_12 (and_12_out, not_15_out, comparator_2_eq, not_16_out, Instruction[3], not_17_out, not_18_out);
  and and_13 (and_13_out, comparator_2_eq, Instruction[3], Instruction[2]);
  and and_14 (ALUvMEMselect, not_19_out, Instruction[31]);
  and and_15 (we_mem, Instruction[29], Instruction[31]);
  and and_16 (BEQ, not_20_out, Instruction[28]);
  and and_17 (BNE, Instruction[26], Instruction[28]);
  and and_18 (and_18_out, not_21_out, Instruction[27], not_22_out);
  and and_19 (and_19_out, not_23_out, Instruction[27], Instruction[26]);
  or or_1 (or_1_out, and_8_out, and_7_out);
  Multiplexer #(.width(5)) multiplexer_2 (
    .in0(Instruction[25:21]), .in1(Instruction[20:16]), .out(rs_select), .sel(or_1_out));
  or or_2 (or_2_out, and_19_out, and_18_out);
  Multiplexer #(.width(16)) multiplexer_3 (
    .in0(multiplexer_1_out), .in1(bit_extender_1_out), .out(imm), .sel(or_2_out));
  not not_24 (not_24_out, comparator_2_eq);
  Multiplexer #(.width(5)) multiplexer_4 (
    .in0(Instruction[15:11]), .in1(Instruction[20:16]), .out(multiplexer_4_out), .sel(not_24_out));
  or or_3 (or_3_out, and_19_out, and_11_out);
  Multiplexer #(.width(5)) multiplexer_5 (.in0(multiplexer_4_out), .in1({5{1'b1}}), .out(rd_select), .sel(or_3_out));
  assign bit_extender_3_out = {{3{1'b0}}, and_2_out};  // Bit_Extender bit_extender_3
  assign bit_extender_4_out = {{3{1'b0}}, and_3_out};  // Bit_Extender bit_extender_4
  assign bit_extender_5_out = {{3{1'b0}}, and_4_out};  // Bit_Extender bit_extender_5
  assign bit_extender_6_out = {{3{1'b0}}, and_5_out};  // Bit_Extender bit_extender_6
  assign bit_extender_7_out = {{3{1'b0}}, and_6_out};  // Bit_Extender bit_extender_7
  assign bit_extender_8_out = {{3{1'b0}}, and_7_out};  // Bit_Extender bit_extender_8
  assign bit_extender_9_out = {{3{1'b0}}, and_8_out};  // Bit_Extender bit_extender_9
  assign bit_extender_10_out = {{3{1'b0}}, and_9_out};  // Bit_Extender bit_extender_10
  Multiplier #(.width(4)) multiplier_1 (
    .a(bit_extender_3_out), .b(4'b0001), .out(multiplier_1_out));  // open: cin, cout
  Multiplier #(.width(4)) multiplier_2 (
    .a(bit_extender_4_out), .b(4'b0010), .out(multiplier_2_out));  // open: cin, cout
  Multiplier #(.width(4)) multiplier_3 (
    .a(bit_extender_5_out), .b(4'b0011), .out(multiplier_3_out));  // open: cin, cout
  Multiplier #(.width(4)) multiplier_4 (
    .a(bit_extender_6_out), .b(4'b0100), .out(multiplier_4_out));  // open: cin, cout
  Multiplier #(.width(4)) multiplier_5 (
    .a(bit_extender_7_out), .b(4'b0101), .out(multiplier_5_out));  // open: cin, cout
  Multiplier #(.width(4)) multiplier_6 (
    .a(bit_extender_8_out), .b(4'b0110), .out(multiplier_6_out));  // open: cin, cout
  Multiplier #(.width(4)) multiplier_7 (
    .a(bit_extender_9_out), .b(4'b0111), .out(multiplier_7_out));  // open: cin, cout
  Multiplier #(.width(4)) multiplier_8 (
    .a(bit_extender_10_out), .b(4'b1000), .out(multiplier_8_out));  // open: cin, cout
  not not_25 (not_25_out, BNE);
  and and_20 (and_20_out, not_25_out, not_26_out);
  not not_26 (not_26_out, BEQ);
  not not_27 (not_27_out, comparator_2_eq);
  or or_4 (or_4_out, and_7_out, and_8_out, not_27_out);
  nor nor_1 (nor_1_out, and_3_out, and_4_out);
  or or_5 (ALUvsPCselect, and_19_out, and_13_out, and_11_out);
  Adder #(.width(4)) adder_1 (.a(multiplier_1_out), .b(multiplier_2_out), .out(adder_1_out));  // open: cin, cout
  Adder #(.width(4)) adder_2 (.a(multiplier_3_out), .b(multiplier_4_out), .out(adder_2_out));  // open: cin, cout
  Adder #(.width(4)) adder_3 (.a(multiplier_5_out), .b(multiplier_6_out), .out(adder_3_out));  // open: cin, cout
  Adder #(.width(4)) adder_4 (.a(multiplier_7_out), .b(multiplier_8_out), .out(adder_4_out));  // open: cin, cout
  Adder #(.width(4)) adder_5 (.a(adder_1_out), .b(adder_2_out), .out(adder_5_out));  // open: cin, cout
  Adder #(.width(4)) adder_6 (.a(adder_3_out), .b(adder_4_out), .out(adder_6_out));  // open: cin, cout
  and and_21 (imm_sel, and_20_out, or_4_out);
  and and_22 (and_22_out, nor_1_out, comparator_2_eq);
  or or_6 (or_6_out, and_10_out, ALUvMEMselect, and_13_out, and_19_out, and_11_out);
  or or_7 (J_Jal, and_19_out, and_18_out);
  or or_8 (Jr_Jalr, and_11_out, and_12_out);
  or or_9 (or_9_out, and_22_out, or_6_out);
  Adder #(.width(4)) adder_7 (.a(adder_5_out), .b(adder_6_out), .out(ALU_operation));  // open: cin, cout
  and and_23 (we_regfile, or_9_out, not_1_out);

  assign rt_select = Instruction[20:16];

  // Notes on the sheet:
  //   OPCODE
  //   FUNC CODE
  //   ADD
  //   SUB
  //   MULT
  //   DIV
  //   MFLO
  //   MFHI
  //   SRL
  //   SLL
  //   SLT
  //   ADDI
  //   JALR
  //   JR
  //   SYSCALL
  //   LW
  //   SW
  //   BEQ
  //   BNE
  //   J
  //   JAL
endmodule
