// Logisim project ProjectBusLayout.circ as structural Verilog: 16 circuits, main circuit Computer
module Computer (
);

  wire button_1_out, buttoncontroller_1_writeenabletobus, buzzercontroller_1_writeenabletobuzzer,
       clock_1_out, clock_2_out, clock_3_out, cpu_1_buswriteenable, joystickcontroller_1_writeenabletobus,
       keyboard_1_avail, keyboardcontroller_1_keyboardread, keyboardcontroller_1_writetobus,
       ledcontroller_1_light, memorycontroller_1_writeenabletomem, memorycontroller_1_writetobus,
       rgb_video_1_p1, rgb_video_1_p2, rgbledcontroller_1_blue, rgbledcontroller_1_green,
       rgbledcontroller_1_red, slidercontroller_1_writeenabletobus, switch_1_p1, switch_1_p2,
       switchcontroller_1_writeenabletobus, terminalcontroller_1_clearsscreen,
       terminalcontroller_1_writetoterminal;
  wire [3:0] joystick_1_x, joystick_1_y;
  wire [6:0] buzzercontroller_1_buzzervolume, keyboard_1_data, terminalcontroller_1_datatoterminal;
  wire [7:0] buzzercontroller_1_buzzerdutycycle, rgb_video_1_p3, rgb_video_1_p4, slider_1_out;
  wire [13:0] buzzercontroller_1_buzzerfrequency;
  wire [23:0] memorycontroller_1_addresstomem, rgb_video_1_p5;
  wire [25:0] cpu_1_addresstobus;
  wire [31:0] buttoncontroller_1_datatobus, controlled_buffer_1_out, cpu_1_datatobus,
       joystickcontroller_1_datatobus, keyboardcontroller_1_datatobus, memorycontroller_1_datatobus,
       memorycontroller_1_datatomem, ram_1_dout, slidercontroller_1_datatobus, switchcontroller_1_datatobus;

  RAM #(.addrWidth(24), .dataWidth(32), .enables("line")) ram_1 (
    .addr(memorycontroller_1_addresstomem), .we(memorycontroller_1_writeenabletomem), .clk(clock_1_out),
    .din(memorycontroller_1_datatomem), .dout(ram_1_dout));
  Clock clock_1 (.out(clock_1_out));
  Joystick joystick_1 (.x(joystick_1_x), .y(joystick_1_y));
  Button button_1 (.out(button_1_out));
  Slider slider_1 (.out(slider_1_out));
  // Switch switch_1: pin names not known; wires that end beside it: switch_1_p1, switch_1_p2
  Clock clock_2 (.out(clock_2_out));
  Keyboard keyboard_1 (
    .clk(clock_2_out), .re(keyboardcontroller_1_keyboardread), .avail(keyboard_1_avail),
    .data(keyboard_1_data));  // open: clr
  MemoryController memorycontroller_1 (
    .WriteEnableFromBus(cpu_1_buswriteenable), .AddressFromBus(cpu_1_addresstobus), .DataFromMem(ram_1_dout),
    .DataFromBus(controlled_buffer_1_out), .WriteEnableToMem(memorycontroller_1_writeenabletomem),
    .DataToBus(memorycontroller_1_datatobus), .AddressToMem(memorycontroller_1_addresstomem),
    .DataToMem(memorycontroller_1_datatomem), .WriteToBus(memorycontroller_1_writetobus));
  CPU cpu_1 (
    .DataFromBus(controlled_buffer_1_out), .AddressToBus(cpu_1_addresstobus),
    .BusWriteEnable(cpu_1_buswriteenable), .DataToBus(cpu_1_datatobus));
  JoyStickController joystickcontroller_1 (
    .DataFromBus(controlled_buffer_1_out), .WriteEnableFromBus(cpu_1_buswriteenable),
    .AddressFromBus(cpu_1_addresstobus), .X(joystick_1_x), .Y(joystick_1_y),
    .WriteEnableToBus(joystickcontroller_1_writeenabletobus), .DataToBus(joystickcontroller_1_datatobus));
  ButtonController buttoncontroller_1 (
    .DataFromBus(controlled_buffer_1_out), .WriteEnableFromBus(cpu_1_buswriteenable),
    .AddressFromBus(cpu_1_addresstobus), .Button(button_1_out),
    .WriteEnableToBus(buttoncontroller_1_writeenabletobus), .DataToBus(buttoncontroller_1_datatobus));
  SwitchController switchcontroller_1 (
    .DataFromBus(controlled_buffer_1_out), .WriteEnableFromBus(cpu_1_buswriteenable),
    .AddressFromBus(cpu_1_addresstobus), .SwitchValue(switch_1_p2),
    .WriteEnableToBus(switchcontroller_1_writeenabletobus), .DataToBus(switchcontroller_1_datatobus),
    .DataToSwitch(switch_1_p1));
  SliderController slidercontroller_1 (
    .DataFromBus(controlled_buffer_1_out), .AddressFromBus(cpu_1_addresstobus),
    .WriteEnableFromBus(cpu_1_buswriteenable), .DataFromSlider(slider_1_out),
    .WriteEnableToBus(slidercontroller_1_writeenabletobus), .DataToBus(slidercontroller_1_datatobus));
  assign controlled_buffer_1_out = memorycontroller_1_writetobus ? memorycontroller_1_datatobus : 32'bz;  // Controlled_Buffer controlled_buffer_1
  assign controlled_buffer_1_out = cpu_1_buswriteenable ? cpu_1_datatobus : 32'bz;  // Controlled_Buffer controlled_buffer_2
  KeyboardController keyboardcontroller_1 (
    .KeyboardData(keyboard_1_data), .KeyboardStatus(keyboard_1_avail), .DataFromBus(controlled_buffer_1_out),
    .WriteEnableFromBus(cpu_1_buswriteenable), .AddressFromBus(cpu_1_addresstobus),
    .WriteToBus(keyboardcontroller_1_writetobus), .KeyboardRead(keyboardcontroller_1_keyboardread),
    .DataToBus(keyboardcontroller_1_datatobus));
  assign controlled_buffer_1_out = keyboardcontroller_1_writetobus ? keyboardcontroller_1_datatobus : 32'bz;  // Controlled_Buffer controlled_buffer_3
  assign controlled_buffer_1_out = joystickcontroller_1_writeenabletobus ? joystickcontroller_1_datatobus : 32'bz;  // Controlled_Buffer controlled_buffer_4
  assign controlled_buffer_1_out = buttoncontroller_1_writeenabletobus ? buttoncontroller_1_datatobus : 32'bz;  // Controlled_Buffer controlled_buffer_5
  assign controlled_buffer_1_out = switchcontroller_1_writeenabletobus ? switchcontroller_1_datatobus : 32'bz;  // Controlled_Buffer controlled_buffer_6
  assign controlled_buffer_1_out = slidercontroller_1_writeenabletobus ? slidercontroller_1_datatobus : 32'bz;  // Controlled_Buffer controlled_buffer_7
  Clock clock_3 (.out(clock_3_out));
  TTY tty_1 (
    .data(terminalcontroller_1_datatoterminal), .clk(clock_3_out), .we(terminalcontroller_1_writetoterminal),
    .clr(terminalcontroller_1_clearsscreen));
  // RGB_Video #(.height(256), .scale(1), .width(256)) rgb_video_1: pin names not known; wires that end beside it: rgb_video_1_p1, rgb_video_1_p2, rgb_video_1_p3, rgb_video_1_p4, rgb_video_1_p5
  Clock clock_4 (.out(rgb_video_1_p1));
  TerminalController terminalcontroller_1 (
    .WriteEnableFromBus(cpu_1_buswriteenable), .AddressFromBus(cpu_1_addresstobus),
    .DataFromBus(controlled_buffer_1_out), .DataToTerminal(terminalcontroller_1_datatoterminal),
    .WriteToTerminal(terminalcontroller_1_writetoterminal), .ClearsScreen(terminalcontroller_1_clearsscreen));
  RGBController rgbcontroller_1 (
    .AddressFromBus(cpu_1_addresstobus), .DataFromBus(controlled_buffer_1_out),
    .WriteEnable(cpu_1_buswriteenable), .RGBX(rgb_video_1_p3), .RGBY(rgb_video_1_p4),
    .RGBColor(rgb_video_1_p5), .RGBWrite(rgb_video_1_p2));
  LEDController ledcontroller_1 (
    .WriteEnable(cpu_1_buswriteenable), .AddressFromBus(cpu_1_addresstobus),
    .DataFromBus(controlled_buffer_1_out), .Light(ledcontroller_1_light));
  RGBLEDController rgbledcontroller_1 (
    .AddressFromBus(cpu_1_addresstobus), .DataFromBus(controlled_buffer_1_out),
    .WriteEnable(cpu_1_buswriteenable), .Green(rgbledcontroller_1_green), .Red(rgbledcontroller_1_red),
    .Blue(rgbledcontroller_1_blue));
  LED led_1 (.in(ledcontroller_1_light));
  BuzzerController buzzercontroller_1 (
    .DataFromBus(controlled_buffer_1_out), .AddressFromBus(cpu_1_addresstobus),
    .WriteEnable(cpu_1_buswriteenable), .BuzzerFrequency(buzzercontroller_1_buzzerfrequency),
    .WriteEnableToBuzzer(buzzercontroller_1_writeenabletobuzzer),
    .BuzzerVolume(buzzercontroller_1_buzzervolume), .BuzzerDutyCycle(buzzercontroller_1_buzzerdutycycle));
  // RGBLED rgbled_1: pin names not known; wires that end beside it: rgbledcontroller_1_red, rgbledcontroller_1_green, rgbledcontroller_1_blue
  // Buzzer buzzer_1: pin names not known; wires that end beside it: buzzercontroller_1_buzzerfrequency, buzzercontroller_1_writeenabletobuzzer, buzzercontroller_1_buzzervolume, buzzercontroller_1_buzzerdutycycle

  // Notes on the sheet:
  //   Write_enable
  //   Address
  //   Data
endmodule

module CPU (
  input  [31:0] DataFromBus,
  output [31:0] DataToBus,
  output BusWriteEnable,
  output [25:0] AddressToBus
);

  wire alu_1_equal, and_1_out, and_2_out, clock_1_out, control_1_aluvmemselect, control_1_aluvspcselect,
       control_1_anyjsel, control_1_beq, control_1_bne, control_1_imm_sel, control_1_jr_jalr,
       control_1_we_regfile, not_1_out, or_1_out;
  wire [3:0] control_1_alu_operation;
  wire [4:0] control_1_rd_select, control_1_rs_select, control_1_rt_select;
  wire [15:0] bit_extender_3_out, control_1_imm, shifter_1_out;
  wire [25:0] bit_extender_4_out, shifter_2_out;
  wire [31:0] adder_1_out, adder_2_out, alu_1_res, bit_extender_1_out, bit_extender_2_out,
       bit_extender_5_out, multiplexer_1_out, multiplexer_2_out, multiplexer_3_out, multiplexer_4_out,
       multiplexer_5_out, multiplexer_6_out, ProgramCounter_q, regfile_1_data_rs, rom_1_data, shifter_3_out;

  Shifter #(.width(16)) shifter_1 (.in(control_1_imm), .\dist (4'b0010), .out(shifter_1_out));
  Adder #(.width(32)) adder_1 (.a(ProgramCounter_q), .b(32'h4), .out(adder_1_out));  // open: cin, cout
  assign bit_extender_1_out = {{16{shifter_1_out[15]}}, shifter_1_out};  // Bit_Extender bit_extender_1
  Multiplexer #(.width(32)) multiplexer_1 (
    .in0(adder_1_out), .in1(adder_2_out), .out(multiplexer_1_out), .sel(or_1_out));
  Adder #(.width(32)) adder_2 (.a(adder_1_out), .b(bit_extender_1_out), .out(adder_2_out));  // open: cin, cout
  assign bit_extender_2_out = {{6{shifter_2_out[25]}}, shifter_2_out};  // Bit_Extender bit_extender_2
  Shifter #(.width(26)) shifter_2 (.in(bit_extender_4_out), .\dist (5'b00010), .out(shifter_2_out));
  or or_1 (or_1_out, and_2_out, and_1_out);
  Multiplexer #(.width(32)) multiplexer_2 (
    .in0(bit_extender_2_out), .in1(regfile_1_data_rs), .out(multiplexer_2_out), .sel(control_1_jr_jalr));
  and and_1 (and_1_out, alu_1_equal, control_1_beq);
  Shifter #(.shift("lr"), .width(32)) shifter_3 (.in(ProgramCounter_q), .\dist (5'b00010), .out(shifter_3_out));
  Register #(.width(32)) ProgramCounter (
    .D(multiplexer_3_out), .en(1'b1), .clk(clock_1_out), .Q(ProgramCounter_q));  // open: clr
  Multiplexer #(.width(32)) multiplexer_3 (
    .in0(multiplexer_1_out), .in1(multiplexer_2_out), .out(multiplexer_3_out), .sel(control_1_anyjsel));
  Clock clock_1 (.out(clock_1_out));
  and and_2 (and_2_out, control_1_bne, not_1_out);
  not not_1 (not_1_out, alu_1_equal);
  Bit_Extender #(.in_width(32)) bit_extender_3 (.in(shifter_3_out), .out(bit_extender_3_out));
  ROM #(.addrWidth(16), .dataWidth(32)) rom_1 (.addr(bit_extender_3_out), .data(rom_1_data));
  // Probe on rom_1_data
  Bit_Extender #(.in_width(32), .out_width(26)) bit_extender_4 (.in(rom_1_data), .out(bit_extender_4_out));
  Multiplexer #(.width(32)) multiplexer_4 (
    .in0(alu_1_res), .in1(DataFromBus), .out(multiplexer_4_out), .sel(control_1_aluvmemselect));
  Multiplexer #(.width(32)) multiplexer_5 (
    .in0(multiplexer_4_out), .in1(adder_1_out), .out(multiplexer_5_out), .sel(control_1_aluvspcselect));
  Control control_1 (
    .Instruction(rom_1_data), .imm(control_1_imm), .rd_select(control_1_rd_select),
    .rt_select(control_1_rt_select), .rs_select(control_1_rs_select),
    .ALU_operation(control_1_alu_operation), .imm_sel(control_1_imm_sel), .we_regfile(control_1_we_regfile),
    .we_mem(BusWriteEnable), .ALUvMEMselect(control_1_aluvmemselect),
    .ALUvsPCselect(control_1_aluvspcselect), .AnyJsel(control_1_anyjsel), .BEQ(control_1_beq),
    .BNE(control_1_bne), .Jr_Jalr(control_1_jr_jalr));
  regfile regfile_1 (
    .w_e(control_1_we_regfile), .rs(control_1_rs_select), .data_in(multiplexer_5_out),
    .rd(control_1_rd_select), .rt(control_1_rt_select), .data_rs(regfile_1_data_rs), .data_rt(DataToBus));
  assign bit_extender_5_out = {{16{control_1_imm[15]}}, control_1_imm};  // Bit_Extender bit_extender_5
  Multiplexer #(.width(32)) multiplexer_6 (
    .in0(DataToBus), .in1(bit_extender_5_out), .out(multiplexer_6_out), .sel(control_1_imm_sel));
  ALU alu_1 (
    .operation(control_1_alu_operation), .op1(regfile_1_data_rs), .op2(multiplexer_6_out), .Res(alu_1_res),
    .equal(alu_1_equal));
  Bit_Extender #(.in_width(32), .out_width(26)) bit_extender_6 (.in(alu_1_res), .out(AddressToBus));

  // Notes on the sheet:
  //   offset: (word addressed)
  //   PC + 4
  //   label: for j, jal (word addressed)
  //   PC + 4 + Offset
  //   register: for jr, jalr (byte addressed)
  //   jr/jalr
  //   any j*
  //   immediate
  //   label to jump to
  //   rs-data
  //   contents of rom_1 (hex, n*v repeats v):
  //   1040001f 201b0001 105b0021 201b0005 105b0047 201b0009 105b0065 201b000a 105b0067 201b000b 105b0066
  //   201b000c 105b0066 201b000d 105b0069 201b000f 105b0069 201b0010 105b0069 201b0011 105b0069 201b0012
  //   105b0069 201b0013 105b0069 201b0014 105b006c 201b0015 105b006c 201b0016 105bffe0 8000070 201df000
  //   201b0000 ac1bfefc 800008b 23bdffec afa80000 afa90004 afaa0008 afab000c afac0010 20880000 200b000a
  //   200c000a 100482a 11200005 2009002d ac09ff00 2009ffff 1280018 4012 10c001a 4812 11200003 18b0018 6012
  //   8000034 18b001a 6012 10c001a 4812 21290030 ac09ff00 4010 18b001a 6012 11800001 800003c 8fa80000
  //   8fa90004 8faa0008 8fab000c 8fac0010 23bd0014 3400008 8c1bff10 1360fffe 23bdffec afa80000 afa90004
  //   afaa0008 afab000c afac0010 2008000a 200a0030 200b003a 20020000 20030000 8c09ff14 12a602a 15800009
  //   12b602a 11800007 20030001 ac09ff10 480018 1012 491020 2042ffd0 8000059 8fa80000 8fa90004 8faa0008
  //   8fab000c 8fac0010 23bd0014 3400008 8c02fefc 44d820 ac1bfefc 3400008 8000070 ac04ff00 3400008
  //   8c1bff10 1360fffc 8c02ff14 ac1bff10 3400008 8c1bff04 3400008 ac04ff30 3400008 ac04ff40 3400008
  //   8c820000 3400008 8c02ff60 3400008 10a00002 ac04ff74 3400008 8c02ff70 3400008 8c02ff90 3400008
  //   aca40000 3400008 23bdffd0 200800ff 84a00 85400 200b007f b6200 b6c00 afaa0000 14cc020 afb80004
  //   149c020 afb80008 1a9c020 afb8000c afa90010 169c020 afb80014 109c020 afb80018 10cc020 afb8001c
  //   afa80020 10dc020 afb80024 10ac020 afb80028 16ac020 afb8002c 20100080 2011007e 20120040 2013003f
  //   20140001 20150000 2110018 4012 84080 82020 20020009 d00c 40b020 20170000 200f0061 8c08ff10 11000004
  //   2002000c d00c 407820 ac00ff10 20090061 15e90004 12400015 2014ffff 20150000 80000d4 20090064 15e90004
  //   1250000f 20140001 20150000 80000d4 20090073 15e90004 12710009 20140000 20150001 80000d4 20090077
  //   15e90004 12600003 20140000 2015ffff 80000d4 2549020 2759820 2700018 4012 1124020 84080 1164020
  //   8d090000 200a0001 112a0015 ad0a0000 240402a 15000012 212402a 15000010 260402a 1500000e 233402a
  //   1500000c 22f70001 2009000c 2e9001a b810 174880 13d4820 8d290000 ac12ff20 ac13ff24 ac09ff28 ac00ff2c
  //   80000b6 2002000b 20040059 d00c 2004004f d00c 20040055 d00c 20040020 d00c 2004004c d00c 2004004f d00c
  //   20040053 d00c 20040045 d00c 20040020 d00c 2004003c d00c 20040033 d00c 2002000a d00c
  //   probe to help test the value in a wire
  //   ALU
  //   PC + 4
  //   MEM
  //   jal/jalr
  //   value from memory
  //   1 if two registers are ==
  //   value from ALU
endmodule

module MemoryController (
  input  WriteEnableFromBus,
  input  [25:0] AddressFromBus,
  input  [31:0] DataFromBus,
  input  [31:0] DataFromMem,
  output [31:0] DataToBus,
  output WriteToBus,
  output WriteEnableToMem,
  output [23:0] AddressToMem,
  output [31:0] DataToMem
);

  wire comparator_1_lt, not_1_out;
  wire [25:0] shifter_1_out;

  Comparator #(.mode("unsigned"), .width(26)) comparator_1 (
    .a(AddressFromBus), .b(26'h3ffff00), .lt(comparator_1_lt));  // open: gt, eq
  not not_1 (not_1_out, WriteEnableFromBus);
  and and_1 (WriteToBus, not_1_out, comparator_1_lt);
  and and_2 (WriteEnableToMem, WriteEnableFromBus, comparator_1_lt);
  Shifter #(.shift("lr"), .width(26)) shifter_1 (.in(AddressFromBus), .\dist (5'b00010), .out(shifter_1_out));
  Bit_Extender #(.in_width(26), .out_width(24)) bit_extender_1 (.in(shifter_1_out), .out(AddressToMem));

  assign DataToBus = DataFromMem;
  assign DataToMem = DataFromBus;
endmodule

module KeyboardController (
  input  [31:0] DataFromBus,
  input  WriteEnableFromBus,
  input  [25:0] AddressFromBus,
  input  [6:0] KeyboardData,
  input  KeyboardStatus,
  output WriteToBus,
  output [31:0] DataToBus,
  output KeyboardRead
);

  wire and_1_out, and_3_out, comparator_1_eq, comparator_2_eq, not_1_out, not_2_out;
  wire [31:0] bit_extender_1_out, bit_extender_2_out;

  Comparator #(.mode("unsigned"), .width(26)) comparator_1 (
    .a(AddressFromBus), .b(26'h3ffff10), .eq(comparator_1_eq));  // open: gt, lt
  Comparator #(.mode("unsigned"), .width(26)) comparator_2 (
    .a(AddressFromBus), .b(26'h3ffff14), .eq(comparator_2_eq));  // open: gt, lt
  not not_1 (not_1_out, WriteEnableFromBus);
  not not_2 (not_2_out, WriteEnableFromBus);
  and and_1 (and_1_out, not_2_out, comparator_1_eq);
  and and_2 (KeyboardRead, WriteEnableFromBus, comparator_1_eq);
  and and_3 (and_3_out, not_1_out, comparator_2_eq);
  or or_1 (WriteToBus, and_1_out, and_3_out);
  assign bit_extender_1_out = {{25{1'b0}}, KeyboardData};  // Bit_Extender bit_extender_1
  assign bit_extender_2_out = {{31{1'b0}}, KeyboardStatus};  // Bit_Extender bit_extender_2
  Multiplexer #(.width(32)) multiplexer_1 (
    .in0(bit_extender_1_out), .in1(bit_extender_2_out), .out(DataToBus), .sel(and_1_out));
endmodule

module RGBController (
  input  [25:0] AddressFromBus,
  input  [31:0] DataFromBus,
  input  WriteEnable,
  output [7:0] RGBX,
  output [7:0] RGBY,
  output [23:0] RGBColor,
  output RGBWrite
);

  wire and_1_out, and_2_out, and_3_out, clock_1_out, comparator_1_eq, comparator_2_eq, comparator_3_eq,
       comparator_4_eq;
  wire [7:0] bit_extender_1_out, bit_extender_2_out;
  wire [23:0] bit_extender_3_out;

  Comparator #(.width(26)) comparator_1 (.a(AddressFromBus), .b(26'h3ffff20), .eq(comparator_1_eq));  // open: gt, lt
  Comparator #(.width(26)) comparator_2 (.a(AddressFromBus), .b(26'h3ffff24), .eq(comparator_2_eq));  // open: gt, lt
  Comparator #(.width(26)) comparator_3 (.a(AddressFromBus), .b(26'h3ffff28), .eq(comparator_3_eq));  // open: gt, lt
  Comparator #(.width(26)) comparator_4 (.a(AddressFromBus), .b(26'h3ffff2c), .eq(comparator_4_eq));  // open: gt, lt
  and and_1 (and_1_out, WriteEnable, comparator_1_eq);
  and and_2 (and_2_out, WriteEnable, comparator_2_eq);
  and and_3 (and_3_out, WriteEnable, comparator_3_eq);
  and and_4 (RGBWrite, WriteEnable, comparator_4_eq);
  Clock clock_1 (.out(clock_1_out));
  Register X (.D(bit_extender_1_out), .en(and_1_out), .clk(clock_1_out), .Q(RGBX));  // open: clr
  Bit_Extender #(.in_width(32), .out_width(8), .\type ("zero")) bit_extender_1 (
    .in(DataFromBus), .out(bit_extender_1_out));
  Register Y (.D(bit_extender_2_out), .en(and_2_out), .clk(clock_1_out), .Q(RGBY));  // open: clr
  Bit_Extender #(.in_width(32), .out_width(8), .\type ("zero")) bit_extender_2 (
    .in(DataFromBus), .out(bit_extender_2_out));
  Register #(.width(24)) Pixel (.D(bit_extender_3_out), .en(and_3_out), .clk(clock_1_out), .Q(RGBColor));  // open: clr
  Bit_Extender #(.in_width(32), .out_width(24), .\type ("zero")) bit_extender_3 (
    .in(DataFromBus), .out(bit_extender_3_out));
endmodule

module TerminalController (
  input  WriteEnableFromBus,
  input  [25:0] AddressFromBus,
  input  [31:0] DataFromBus,
  output [6:0] DataToTerminal,
  output WriteToTerminal,
  output ClearsScreen
);

  wire comparator_1_eq, comparator_2_eq, not_1_out;

  Comparator #(.width(26)) comparator_1 (.a(AddressFromBus), .b(26'h3ffff00), .eq(comparator_1_eq));  // open: gt, lt
  Comparator #(.mode("unsigned"), .width(26)) comparator_2 (
    .a(AddressFromBus), .b(26'h3ffff04), .eq(comparator_2_eq));  // open: gt, lt
  and and_1 (WriteToTerminal, WriteEnableFromBus, comparator_1_eq);
  not not_1 (not_1_out, WriteEnableFromBus);
  and and_2 (ClearsScreen, not_1_out, comparator_2_eq);
  Bit_Extender #(.in_width(32), .out_width(7), .\type ("zero")) bit_extender_1 (.in(DataFromBus), .out(DataToTerminal));
endmodule

module regfile (
  input  w_e,
  input  [4:0] rs,
  input  [31:0] data_in,
  input  [4:0] rd,
  input  [4:0] rt,
  output [31:0] data_rs,
  output [31:0] data_rt
);

  wire clock_1_out, demultiplexer_1_out1, demultiplexer_1_out2, demultiplexer_1_out3, demultiplexer_1_out4,
       demultiplexer_1_out5, demultiplexer_1_out6, demultiplexer_1_out7, demultiplexer_1_out8,
       demultiplexer_1_out9, demultiplexer_1_out10, demultiplexer_1_out11, demultiplexer_1_out12,
       demultiplexer_1_out13, demultiplexer_1_out14, demultiplexer_1_out15, demultiplexer_1_out16,
       demultiplexer_1_out17, demultiplexer_1_out18, demultiplexer_1_out19, demultiplexer_1_out20,
       demultiplexer_1_out21, demultiplexer_1_out22, demultiplexer_1_out23, demultiplexer_1_out24,
       demultiplexer_1_out25, demultiplexer_1_out26, demultiplexer_1_out27, demultiplexer_1_out28,
       demultiplexer_1_out29, demultiplexer_1_out30, demultiplexer_1_out31;
  wire [31:0] a0_q, a1_q, a2_q, a3_q, at_q, demultiplexer_2_out1, demultiplexer_2_out2, demultiplexer_2_out3,
       demultiplexer_2_out4, demultiplexer_2_out5, demultiplexer_2_out6, demultiplexer_2_out7,
       demultiplexer_2_out8, demultiplexer_2_out9, demultiplexer_2_out10, demultiplexer_2_out11,
       demultiplexer_2_out12, demultiplexer_2_out13, demultiplexer_2_out14, demultiplexer_2_out15,
       demultiplexer_2_out16, demultiplexer_2_out17, demultiplexer_2_out18, demultiplexer_2_out19,
       demultiplexer_2_out20, demultiplexer_2_out21, demultiplexer_2_out22, demultiplexer_2_out23,
       demultiplexer_2_out24, demultiplexer_2_out25, demultiplexer_2_out26, demultiplexer_2_out27,
       demultiplexer_2_out28, demultiplexer_2_out29, demultiplexer_2_out30, demultiplexer_2_out31, gp_q,
       k0_q, k1_q, ra_q, s0_q, s1_q, s2_q, s3_q, s4_q, s5_q, s6_q, s7_q, s8_q, sp_q, t0_q, t1_q, t2_q, t3_q,
       t4_q, t5_q, t6_q, t7_q, t8_q, t9_q, v0_q, v1_q;

  Demultiplexer #(.select(5)) demultiplexer_1 (
    .out1(demultiplexer_1_out1), .out2(demultiplexer_1_out2), .out3(demultiplexer_1_out3),
    .out4(demultiplexer_1_out4), .out5(demultiplexer_1_out5), .out6(demultiplexer_1_out6),
    .out7(demultiplexer_1_out7), .out8(demultiplexer_1_out8), .out9(demultiplexer_1_out9),
    .out10(demultiplexer_1_out10), .out11(demultiplexer_1_out11), .out12(demultiplexer_1_out12),
    .out13(demultiplexer_1_out13), .out14(demultiplexer_1_out14), .out15(demultiplexer_1_out15),
    .out16(demultiplexer_1_out16), .out17(demultiplexer_1_out17), .out18(demultiplexer_1_out18),
    .out19(demultiplexer_1_out19), .out20(demultiplexer_1_out20), .out21(demultiplexer_1_out21),
    .out22(demultiplexer_1_out22), .out23(demultiplexer_1_out23), .out24(demultiplexer_1_out24),
    .out25(demultiplexer_1_out25), .out26(demultiplexer_1_out26), .out27(demultiplexer_1_out27),
    .out28(demultiplexer_1_out28), .out29(demultiplexer_1_out29), .out30(demultiplexer_1_out30),
    .out31(demultiplexer_1_out31), .in(w_e), .sel(rd));  // open: out0
  Demultiplexer #(.select(5), .width(32)) demultiplexer_2 (
    .out1(demultiplexer_2_out1), .out2(demultiplexer_2_out2), .out3(demultiplexer_2_out3),
    .out4(demultiplexer_2_out4), .out5(demultiplexer_2_out5), .out6(demultiplexer_2_out6),
    .out7(demultiplexer_2_out7), .out8(demultiplexer_2_out8), .out9(demultiplexer_2_out9),
    .out10(demultiplexer_2_out10), .out11(demultiplexer_2_out11), .out12(demultiplexer_2_out12),
    .out13(demultiplexer_2_out13), .out14(demultiplexer_2_out14), .out15(demultiplexer_2_out15),
    .out16(demultiplexer_2_out16), .out17(demultiplexer_2_out17), .out18(demultiplexer_2_out18),
    .out19(demultiplexer_2_out19), .out20(demultiplexer_2_out20), .out21(demultiplexer_2_out21),
    .out22(demultiplexer_2_out22), .out23(demultiplexer_2_out23), .out24(demultiplexer_2_out24),
    .out25(demultiplexer_2_out25), .out26(demultiplexer_2_out26), .out27(demultiplexer_2_out27),
    .out28(demultiplexer_2_out28), .out29(demultiplexer_2_out29), .out30(demultiplexer_2_out30),
    .out31(demultiplexer_2_out31), .in(data_in), .sel(rd));  // open: out0
  Clock clock_1 (.out(clock_1_out));
  Register #(.width(32)) at (
    .D(demultiplexer_2_out1), .en(demultiplexer_1_out1), .clk(clock_1_out), .Q(at_q));  // open: clr
  Register #(.width(32)) v0 (
    .D(demultiplexer_2_out2), .en(demultiplexer_1_out2), .clk(clock_1_out), .Q(v0_q));  // open: clr
  Register #(.width(32)) v1 (
    .D(demultiplexer_2_out3), .en(demultiplexer_1_out3), .clk(clock_1_out), .Q(v1_q));  // open: clr
  Register #(.width(32)) a0 (
    .D(demultiplexer_2_out4), .en(demultiplexer_1_out4), .clk(clock_1_out), .Q(a0_q));  // open: clr
  Register #(.width(32)) a1 (
    .D(demultiplexer_2_out5), .en(demultiplexer_1_out5), .clk(clock_1_out), .Q(a1_q));  // open: clr
  Register #(.width(32)) a2 (
    .D(demultiplexer_2_out6), .en(demultiplexer_1_out6), .clk(clock_1_out), .Q(a2_q));  // open: clr
  Register #(.width(32)) a3 (
    .D(demultiplexer_2_out7), .en(demultiplexer_1_out7), .clk(clock_1_out), .Q(a3_q));  // open: clr
  Register #(.width(32)) t0 (
    .D(demultiplexer_2_out8), .en(demultiplexer_1_out8), .clk(clock_1_out), .Q(t0_q));  // open: clr
  Register #(.width(32)) t1 (
    .D(demultiplexer_2_out9), .en(demultiplexer_1_out9), .clk(clock_1_out), .Q(t1_q));  // open: clr
  Register #(.width(32)) t2 (
    .D(demultiplexer_2_out10), .en(demultiplexer_1_out10), .clk(clock_1_out), .Q(t2_q));  // open: clr
  Register #(.width(32)) t3 (
    .D(demultiplexer_2_out11), .en(demultiplexer_1_out11), .clk(clock_1_out), .Q(t3_q));  // open: clr
  Register #(.width(32)) t4 (
    .D(demultiplexer_2_out12), .en(demultiplexer_1_out12), .clk(clock_1_out), .Q(t4_q));  // open: clr
  Register #(.width(32)) t5 (
    .D(demultiplexer_2_out13), .en(demultiplexer_1_out13), .clk(clock_1_out), .Q(t5_q));  // open: clr
  Register #(.width(32)) t6 (
    .D(demultiplexer_2_out14), .en(demultiplexer_1_out14), .clk(clock_1_out), .Q(t6_q));  // open: clr
  Register #(.width(32)) t7 (
    .D(demultiplexer_2_out15), .en(demultiplexer_1_out15), .clk(clock_1_out), .Q(t7_q));  // open: clr
  Register #(.width(32)) s0 (
    .D(demultiplexer_2_out16), .en(demultiplexer_1_out16), .clk(clock_1_out), .Q(s0_q));  // open: clr
  Register #(.width(32)) s1 (
    .D(demultiplexer_2_out17), .en(demultiplexer_1_out17), .clk(clock_1_out), .Q(s1_q));  // open: clr
  Register #(.width(32)) s2 (
    .D(demultiplexer_2_out18), .en(demultiplexer_1_out18), .clk(clock_1_out), .Q(s2_q));  // open: clr
  Register #(.width(32)) s3 (
    .D(demultiplexer_2_out19), .en(demultiplexer_1_out19), .clk(clock_1_out), .Q(s3_q));  // open: clr
  Register #(.width(32)) s4 (
    .D(demultiplexer_2_out20), .en(demultiplexer_1_out20), .clk(clock_1_out), .Q(s4_q));  // open: clr
  Register #(.width(32)) s5 (
    .D(demultiplexer_2_out21), .en(demultiplexer_1_out21), .clk(clock_1_out), .Q(s5_q));  // open: clr
  Register #(.width(32)) s6 (
    .D(demultiplexer_2_out22), .en(demultiplexer_1_out22), .clk(clock_1_out), .Q(s6_q));  // open: clr
  Register #(.width(32)) s7 (
    .D(demultiplexer_2_out23), .en(demultiplexer_1_out23), .clk(clock_1_out), .Q(s7_q));  // open: clr
  Register #(.width(32)) t8 (
    .D(demultiplexer_2_out24), .en(demultiplexer_1_out24), .clk(clock_1_out), .Q(t8_q));  // open: clr
  Register #(.width(32)) t9 (
    .D(demultiplexer_2_out25), .en(demultiplexer_1_out25), .clk(clock_1_out), .Q(t9_q));  // open: clr
  Register #(.width(32)) k0 (
    .D(demultiplexer_2_out26), .en(demultiplexer_1_out26), .clk(clock_1_out), .Q(k0_q));  // open: clr
  Register #(.width(32)) k1 (
    .D(demultiplexer_2_out27), .en(demultiplexer_1_out27), .clk(clock_1_out), .Q(k1_q));  // open: clr
  Register #(.width(32)) gp (
    .D(demultiplexer_2_out28), .en(demultiplexer_1_out28), .clk(clock_1_out), .Q(gp_q));  // open: clr
  Register #(.width(32)) sp (
    .D(demultiplexer_2_out29), .en(demultiplexer_1_out29), .clk(clock_1_out), .Q(sp_q));  // open: clr
  Register #(.width(32)) s8 (
    .D(demultiplexer_2_out30), .en(demultiplexer_1_out30), .clk(clock_1_out), .Q(s8_q));  // open: clr
  Register #(.width(32)) ra (
    .D(demultiplexer_2_out31), .en(demultiplexer_1_out31), .clk(clock_1_out), .Q(ra_q));  // open: clr
  Multiplexer #(.select(5), .width(32)) multiplexer_1 (
    .in0({32{1'b0}}), .in1(at_q), .in2(v0_q), .in3(v1_q), .in4(a0_q), .in5(a1_q), .in6(a2_q), .in7(a3_q),
    .in8(t0_q), .in9(t1_q), .in10(t2_q), .in11(t3_q), .in12(t4_q), .in13(t5_q), .in14(t6_q), .in15(t7_q),
    .in16(s0_q), .in17(s1_q), .in18(s2_q), .in19(s3_q), .in20(s4_q), .in21(s5_q), .in22(s6_q), .in23(s7_q),
    .in24(t8_q), .in25(t9_q), .in26(k0_q), .in27(k1_q), .in28(gp_q), .in29(sp_q), .in30(s8_q), .in31(ra_q),
    .out(data_rs), .sel(rs));
  Multiplexer #(.select(5), .width(32)) multiplexer_2 (
    .in0({32{1'b0}}), .in1(at_q), .in2(v0_q), .in3(v1_q), .in4(a0_q), .in5(a1_q), .in6(a2_q), .in7(a3_q),
    .in8(t0_q), .in9(t1_q), .in10(t2_q), .in11(t3_q), .in12(t4_q), .in13(t5_q), .in14(t6_q), .in15(t7_q),
    .in16(s0_q), .in17(s1_q), .in18(s2_q), .in19(s3_q), .in20(s4_q), .in21(s5_q), .in22(s6_q), .in23(s7_q),
    .in24(t8_q), .in25(t9_q), .in26(k0_q), .in27(k1_q), .in28(gp_q), .in29(sp_q), .in30(s8_q), .in31(ra_q),
    .out(data_rt), .sel(rt));
endmodule

module ALU (
  input  [3:0] operation,
  input  [31:0] op1,
  input  [31:0] op2,
  output [31:0] Res,
  output equal
);

  wire clock_1_out, comparator_1_lt;
  wire [4:0] bit_extender_1_out, bit_extender_2_out;
  wire [31:0] adder_1_out, bit_extender_3_out, divider_1_out, divider_1_rem, HI_q, LO_q, multiplexer_2_out,
       multiplexer_3_out, multiplier_1_cout, multiplier_1_out, shifter_1_out, shifter_2_out, subtractor_1_out;

  Adder #(.width(32)) adder_1 (.a(op1), .b(op2), .out(adder_1_out));  // open: cin, cout
  Subtractor #(.width(32)) subtractor_1 (.a(op1), .b(op2), .out(subtractor_1_out));  // open: bin, bout
  Multiplier #(.width(32)) multiplier_1 (
    .a(op1), .b(op2), .out(multiplier_1_out), .cout(multiplier_1_cout));  // open: cin
  Divider #(.width(32)) divider_1 (.a(op1), .b(op2), .out(divider_1_out), .rem(divider_1_rem));  // open: upper
  Shifter #(.shift("lr"), .width(32)) shifter_1 (.in(op1), .\dist (bit_extender_1_out), .out(shifter_1_out));
  Bit_Extender #(.in_width(32), .out_width(5), .\type ("zero")) bit_extender_1 (.in(op2), .out(bit_extender_1_out));
  Shifter #(.width(32)) shifter_2 (.in(op1), .\dist (bit_extender_2_out), .out(shifter_2_out));
  Bit_Extender #(.in_width(32), .out_width(5), .\type ("zero")) bit_extender_2 (.in(op2), .out(bit_extender_2_out));
  Comparator #(.width(32)) comparator_1 (.a(op1), .b(op2), .eq(equal), .lt(comparator_1_lt));  // open: gt
  assign bit_extender_3_out = {{31{1'b0}}, comparator_1_lt};  // Bit_Extender bit_extender_3
  Multiplexer #(.select(4), .width(32)) multiplexer_1 (
    .in0(adder_1_out), .in1(subtractor_1_out), .in2(multiplier_1_out), .in3(divider_1_out), .in4(LO_q),
    .in5(HI_q), .in6(shifter_1_out), .in7(shifter_2_out), .in8(bit_extender_3_out), .out(Res), .sel(operation));  // open: in9, in10, in11, in12, in13, in14, in15
  Multiplexer #(.select(4), .width(32)) multiplexer_2 (
    .in0(LO_q), .in1(LO_q), .in2(multiplier_1_out), .in3(divider_1_out), .in4(LO_q), .in5(LO_q), .in6(LO_q),
    .in7(LO_q), .in8(LO_q), .in9(LO_q), .in10(LO_q), .in11(LO_q), .in12(LO_q), .in13(LO_q), .in14(LO_q),
    .in15(LO_q), .out(multiplexer_2_out), .sel(operation));
  Multiplexer #(.select(4), .width(32)) multiplexer_3 (
    .in0(HI_q), .in1(HI_q), .in2(multiplier_1_cout), .in3(divider_1_rem), .in4(HI_q), .in5(HI_q), .in6(HI_q),
    .in7(HI_q), .in8(HI_q), .in9(HI_q), .in10(HI_q), .in11(HI_q), .in12(HI_q), .in13(HI_q), .in14(HI_q),
    .in15(HI_q), .out(multiplexer_3_out), .sel(operation));
  Register #(.width(32)) LO (.D(multiplexer_2_out), .clk(clock_1_out), .Q(LO_q));  // open: en, clr
  Register #(.width(32)) HI (.D(multiplexer_3_out), .clk(clock_1_out), .Q(HI_q));  // open: en, clr
  Clock clock_1 (.out(clock_1_out));
endmodule

module Control (
  input  [31:0] Instruction,
  output [15:0] imm,
  output [4:0] rd_select,
  output [4:0] rt_select,
  output [4:0] rs_select,
  output [3:0] ALU_operation,
  output imm_sel,
  output we_regfile,
  output we_mem,
  output ALUvMEMselect,
  output ALUvsPCselect,
  output AnyJsel,
  output BEQ,
  output BNE,
  output Jr_Jalr
);

  wire and_1_out, and_2_out, and_3_out, and_4_out, and_5_out, and_6_out, and_7_out, and_8_out, and_9_out,
       and_10_out, and_11_out, and_12_out, and_13_out, and_18_out, and_19_out, and_20_out, and_22_out,
       comparator_1_eq, nor_1_out, not_1_out, not_2_out, not_3_out, not_4_out, not_5_out, not_6_out,
       not_7_out, not_8_out, not_9_out, not_10_out, not_11_out, not_12_out, not_13_out, not_14_out,
       not_15_out, not_16_out, not_17_out, not_18_out, not_19_out, not_20_out, not_21_out, not_22_out,
       not_23_out, not_24_out, not_25_out, not_26_out, or_1_out, or_2_out, or_3_out, or_4_out, or_6_out;
  wire [3:0] adder_1_out, adder_2_out, adder_3_out, adder_4_out, adder_5_out, adder_6_out,
       bit_extender_3_out, bit_extender_4_out, bit_extender_5_out, bit_extender_6_out, bit_extender_7_out,
       bit_extender_8_out, bit_extender_9_out, bit_extender_10_out, multiplier_1_out, multiplier_2_out,
       multiplier_3_out, multiplier_4_out, multiplier_5_out, multiplier_6_out, multiplier_7_out,
       multiplier_8_out;
  wire [4:0] multiplexer_4_out;
  wire [15:0] bit_extender_1_out, bit_extender_2_out, multiplexer_1_out;

  Comparator #(.width(6)) comparator_1 (.a(Instruction[31:26]), .b({6{1'b0}}), .eq(comparator_1_eq));  // open: gt, lt
  Bit_Extender #(.in_width(26)) bit_extender_1 (.in(Instruction[25:0]), .out(bit_extender_1_out));
  assign bit_extender_2_out = {{11{1'b0}}, Instruction[10:6]};  // Bit_Extender bit_extender_2
  not not_1 (not_1_out, Instruction[1]);
  not not_2 (not_2_out, Instruction[3]);
  not not_3 (not_3_out, Instruction[1]);
  not not_4 (not_4_out, Instruction[3]);
  not not_5 (not_5_out, Instruction[3]);
  not not_6 (not_6_out, Instruction[1]);
  not not_7 (not_7_out, Instruction[5]);
  not not_8 (not_8_out, Instruction[4]);
  not not_9 (not_9_out, Instruction[4]);
  not not_10 (not_10_out, Instruction[3]);
  not not_11 (not_11_out, Instruction[5]);
  not not_12 (not_12_out, Instruction[1]);
  not not_13 (not_13_out, Instruction[31]);
  not not_14 (not_14_out, Instruction[5]);
  not not_15 (not_15_out, Instruction[4]);
  not not_16 (not_16_out, Instruction[2]);
  not not_17 (not_17_out, Instruction[0]);
  not not_18 (not_18_out, Instruction[29]);
  not not_19 (not_19_out, Instruction[26]);
  not not_20 (not_20_out, Instruction[31]);
  not not_21 (not_21_out, Instruction[26]);
  not not_22 (not_22_out, Instruction[31]);
  Multiplexer #(.width(16)) multiplexer_1 (
    .in0(Instruction[15:0]), .in1(bit_extender_2_out), .out(multiplexer_1_out), .sel(comparator_1_eq));
  and and_1 (and_1_out, not_1_out, Instruction[5], comparator_1_eq);
  and and_2 (and_2_out, Instruction[5], comparator_1_eq, not_2_out, Instruction[1]);
  and and_3 (and_3_out, comparator_1_eq, Instruction[4], Instruction[3], not_3_out);
  and and_4 (and_4_out, comparator_1_eq, Instruction[4], Instruction[3], Instruction[1]);
  and and_5 (and_5_out, comparator_1_eq, Instruction[4], not_4_out, Instruction[1]);
  and and_6 (and_6_out, comparator_1_eq, Instruction[4], not_5_out, not_6_out);
  and and_7 (and_7_out, comparator_1_eq, not_7_out, not_8_out, Instruction[1]);
  and and_8 (and_8_out, comparator_1_eq, not_9_out, not_10_out, not_11_out, not_12_out);
  and and_9 (and_9_out, comparator_1_eq, Instruction[5], Instruction[3], Instruction[1]);
  and and_10 (and_10_out, Instruction[29], not_13_out);
  and and_11 (and_11_out, comparator_1_eq, Instruction[0]);
  and and_12 (and_12_out, not_14_out, comparator_1_eq, not_15_out, Instruction[3], not_16_out, not_17_out);
  and and_13 (and_13_out, comparator_1_eq, Instruction[3], Instruction[2]);
  and and_14 (ALUvMEMselect, not_18_out, Instruction[31]);
  and and_15 (we_mem, Instruction[29], Instruction[31]);
  and and_16 (BEQ, not_19_out, Instruction[28]);
  and and_17 (BNE, Instruction[26], Instruction[28]);
  and and_18 (and_18_out, not_20_out, Instruction[27], not_21_out);
  and and_19 (and_19_out, not_22_out, Instruction[27], Instruction[26]);
  or or_1 (or_1_out, and_8_out, and_7_out);
  Multiplexer #(.width(5)) multiplexer_2 (
    .in0(Instruction[25:21]), .in1(Instruction[20:16]), .out(rs_select), .sel(or_1_out));
  or or_2 (or_2_out, and_19_out, and_18_out);
  Multiplexer #(.width(16)) multiplexer_3 (
    .in0(multiplexer_1_out), .in1(bit_extender_1_out), .out(imm), .sel(or_2_out));
  not not_23 (not_23_out, comparator_1_eq);
  Multiplexer #(.width(5)) multiplexer_4 (
    .in0(Instruction[15:11]), .in1(Instruction[20:16]), .out(multiplexer_4_out), .sel(not_23_out));
  or or_3 (or_3_out, and_19_out, and_11_out);
  Multiplexer #(.width(5)) multiplexer_5 (.in0(multiplexer_4_out), .in1({5{1'b1}}), .out(rd_select), .sel(or_3_out));
  assign bit_extender_3_out = {{3{1'b0}}, and_2_out};  // Bit_Extender bit_extender_3
  assign bit_extender_4_out = {{3{1'b0}}, and_3_out};  // Bit_Extender bit_extender_4
  assign bit_extender_5_out = {{3{1'b0}}, and_4_out};  // Bit_Extender bit_extender_5
  assign bit_extender_6_out = {{3{1'b0}}, and_5_out};  // Bit_Extender bit_extender_6
  assign bit_extender_7_out = {{3{1'b0}}, and_6_out};  // Bit_Extender bit_extender_7
  assign bit_extender_8_out = {{3{1'b0}}, and_7_out};  // Bit_Extender bit_extender_8
  assign bit_extender_9_out = {{3{1'b0}}, and_8_out};  // Bit_Extender bit_extender_9
  assign bit_extender_10_out = {{3{1'b0}}, and_9_out};  // Bit_Extender bit_extender_10
  Multiplier #(.width(4)) multiplier_1 (
    .a(bit_extender_3_out), .b(4'b0001), .out(multiplier_1_out));  // open: cin, cout
  Multiplier #(.width(4)) multiplier_2 (
    .a(bit_extender_4_out), .b(4'b0010), .out(multiplier_2_out));  // open: cin, cout
  Multiplier #(.width(4)) multiplier_3 (
    .a(bit_extender_5_out), .b(4'b0011), .out(multiplier_3_out));  // open: cin, cout
  Multiplier #(.width(4)) multiplier_4 (
    .a(bit_extender_6_out), .b(4'b0100), .out(multiplier_4_out));  // open: cin, cout
  Multiplier #(.width(4)) multiplier_5 (
    .a(bit_extender_7_out), .b(4'b0101), .out(multiplier_5_out));  // open: cin, cout
  Multiplier #(.width(4)) multiplier_6 (
    .a(bit_extender_8_out), .b(4'b0110), .out(multiplier_6_out));  // open: cin, cout
  Multiplier #(.width(4)) multiplier_7 (
    .a(bit_extender_9_out), .b(4'b0111), .out(multiplier_7_out));  // open: cin, cout
  Multiplier #(.width(4)) multiplier_8 (
    .a(bit_extender_10_out), .b(4'b1000), .out(multiplier_8_out));  // open: cin, cout
  not not_24 (not_24_out, BNE);
  and and_20 (and_20_out, not_24_out, not_25_out);
  not not_25 (not_25_out, BEQ);
  not not_26 (not_26_out, comparator_1_eq);
  or or_4 (or_4_out, and_7_out, and_8_out, not_26_out);
  nor nor_1 (nor_1_out, and_3_out, and_4_out);
  or or_5 (ALUvsPCselect, and_19_out, and_13_out, and_11_out);
  Adder #(.width(4)) adder_1 (.a(multiplier_1_out), .b(multiplier_2_out), .out(adder_1_out));  // open: cin, cout
  Adder #(.width(4)) adder_2 (.a(multiplier_3_out), .b(multiplier_4_out), .out(adder_2_out));  // open: cin, cout
  Adder #(.width(4)) adder_3 (.a(multiplier_5_out), .b(multiplier_6_out), .out(adder_3_out));  // open: cin, cout
  Adder #(.width(4)) adder_4 (.a(multiplier_7_out), .b(multiplier_8_out), .out(adder_4_out));  // open: cin, cout
  Adder #(.width(4)) adder_5 (.a(adder_1_out), .b(adder_2_out), .out(adder_5_out));  // open: cin, cout
  Adder #(.width(4)) adder_6 (.a(adder_3_out), .b(adder_4_out), .out(adder_6_out));  // open: cin, cout
  and and_21 (imm_sel, and_20_out, or_4_out);
  and and_22 (and_22_out, nor_1_out, comparator_1_eq);
  or or_6 (or_6_out, and_10_out, ALUvMEMselect, and_13_out, and_19_out, and_11_out);
  or or_7 (AnyJsel, ALUvsPCselect, and_18_out, and_12_out);
  or or_8 (Jr_Jalr, and_11_out, and_13_out, and_12_out);
  or or_9 (we_regfile, and_22_out, or_6_out);
  Adder #(.width(4)) adder_7 (.a(adder_5_out), .b(adder_6_out), .out(ALU_operation));  // open: cin, cout

  assign rt_select = Instruction[20:16];

  // Notes on the sheet:
  //   OPCODE
  //   FUNC CODE
  //   ADD
  //   SUB
  //   MULT
  //   DIV
  //   MFLO
  //   MFHI
  //   SRL
  //   SLL
  //   SLT
  //   ADDI
  //   JALR
  //   JR
  //   SYSCALL
  //   LW
  //   SW
  //   BEQ
  //   BNE
  //   J
  //   JAL
endmodule

module LEDController (
  input  WriteEnable,
  input  [25:0] AddressFromBus,
  input  [31:0] DataFromBus,
  output Light
);

  wire and_1_out, bit_extender_1_out, clock_1_out, comparator_1_eq;

  Bit_Extender #(.in_width(32), .out_width(1), .\type ("zero")) bit_extender_1 (
    .in(DataFromBus), .out(bit_extender_1_out));
  Comparator #(.width(26)) comparator_1 (.a(AddressFromBus), .b(26'h3ffff30), .eq(comparator_1_eq));  // open: gt, lt
  and and_1 (and_1_out, WriteEnable, comparator_1_eq);
  Register #(.width(1)) register_1 (.D(bit_extender_1_out), .en(and_1_out), .clk(clock_1_out), .Q(Light));  // open: clr
  Clock clock_1 (.out(clock_1_out));
endmodule

module RGBLEDController (
  input  [25:0] AddressFromBus,
  input  [31:0] DataFromBus,
  input  WriteEnable,
  output Green,
  output Red,
  output Blue
);

  wire comparator_1_eq, comparator_2_eq, comparator_3_eq, comparator_4_eq;

  Comparator #(.width(26)) comparator_1 (.a(AddressFromBus), .b(26'h3ffff40), .eq(comparator_1_eq));  // open: gt, lt
  Comparator #(.width(32)) comparator_2 (.a(DataFromBus), .b(32'h67), .eq(comparator_2_eq));  // open: gt, lt
  Comparator #(.width(32)) comparator_3 (.a(DataFromBus), .b(32'h72), .eq(comparator_3_eq));  // open: gt, lt
  Comparator #(.width(32)) comparator_4 (.a(DataFromBus), .b(32'h62), .eq(comparator_4_eq));  // open: gt, lt
  and and_1 (Green, WriteEnable, comparator_2_eq, comparator_1_eq);
  and and_2 (Red, WriteEnable, comparator_3_eq, comparator_1_eq);
  and and_3 (Blue, WriteEnable, comparator_4_eq, comparator_1_eq);
endmodule

module JoyStickController (
  input  [31:0] DataFromBus,
  input  WriteEnableFromBus,
  input  [25:0] AddressFromBus,
  input  [3:0] X,
  input  [3:0] Y,
  output WriteEnableToBus,
  output [31:0] DataToBus
);

  wire and_1_out, and_2_out, comparator_1_eq, comparator_2_eq, not_1_out;
  wire [3:0] multiplexer_1_out;

  not not_1 (not_1_out, WriteEnableFromBus);
  Comparator #(.width(26)) comparator_1 (.a(AddressFromBus), .b(26'h3ffff50), .eq(comparator_1_eq));  // open: gt, lt
  Comparator #(.width(26)) comparator_2 (.a(AddressFromBus), .b(26'h3ffff54), .eq(comparator_2_eq));  // open: gt, lt
  and and_1 (and_1_out, not_1_out, comparator_1_eq);
  and and_2 (and_2_out, not_1_out, comparator_2_eq);
  Multiplexer #(.width(4)) multiplexer_1 (.in0(X), .in1(Y), .out(multiplexer_1_out), .sel(and_2_out));
  assign DataToBus = {{28{1'b0}}, multiplexer_1_out};  // Bit_Extender bit_extender_1
  or or_1 (WriteEnableToBus, and_1_out, and_2_out);
endmodule

module ButtonController (
  input  [31:0] DataFromBus,
  input  WriteEnableFromBus,
  input  [25:0] AddressFromBus,
  input  Button,
  output WriteEnableToBus,
  output [31:0] DataToBus
);

  wire comparator_1_eq, not_1_out;

  not not_1 (not_1_out, WriteEnableFromBus);
  Comparator #(.width(26)) comparator_1 (.a(AddressFromBus), .b(26'h3ffff60), .eq(comparator_1_eq));  // open: gt, lt
  assign DataToBus = {{31{1'b0}}, Button};  // Bit_Extender bit_extender_1
  and and_1 (WriteEnableToBus, not_1_out, comparator_1_eq);
endmodule

module SwitchController (
  input  [31:0] DataFromBus,
  input  WriteEnableFromBus,
  input  [25:0] AddressFromBus,
  input  SwitchValue,
  output WriteEnableToBus,
  output [31:0] DataToBus,
  output DataToSwitch
);

  wire and_2_out, bit_extender_1_out, clock_1_out, comparator_1_eq, comparator_2_eq, not_1_out;

  Comparator #(.width(26)) comparator_1 (.a(AddressFromBus), .b(26'h3ffff70), .eq(comparator_1_eq));  // open: gt, lt
  Bit_Extender #(.in_width(32), .out_width(1), .\type ("zero")) bit_extender_1 (
    .in(DataFromBus), .out(bit_extender_1_out));
  not not_1 (not_1_out, WriteEnableFromBus);
  Comparator #(.width(26)) comparator_2 (.a(AddressFromBus), .b(26'h3ffff74), .eq(comparator_2_eq));  // open: gt, lt
  and and_1 (WriteEnableToBus, not_1_out, comparator_1_eq);
  and and_2 (and_2_out, comparator_2_eq, WriteEnableFromBus);
  assign DataToBus = {{31{1'b0}}, SwitchValue};  // Bit_Extender bit_extender_2
  Register #(.width(1)) register_1 (
    .D(bit_extender_1_out), .en(and_2_out), .clk(clock_1_out), .Q(DataToSwitch));  // open: clr
  Clock clock_1 (.out(clock_1_out));
endmodule

module BuzzerController (
  input  [31:0] DataFromBus,
  input  [25:0] AddressFromBus,
  input  WriteEnable,
  output [13:0] BuzzerFrequency,
  output WriteEnableToBuzzer,
  output [6:0] BuzzerVolume,
  output [7:0] BuzzerDutyCycle
);

  wire and_1_out, and_2_out, and_3_out, and_4_out, bit_extender_2_out, clock_1_out, comparator_1_eq,
       comparator_2_eq, comparator_3_eq, comparator_4_eq;
  wire [6:0] bit_extender_3_out;
  wire [7:0] bit_extender_4_out;
  wire [13:0] bit_extender_1_out;

  Comparator #(.mode("unsigned"), .width(26)) comparator_1 (
    .a(AddressFromBus), .b(26'h3ffff80), .eq(comparator_1_eq));  // open: gt, lt
  Comparator #(.mode("unsigned"), .width(26)) comparator_2 (
    .a(AddressFromBus), .b(26'h3ffff84), .eq(comparator_2_eq));  // open: gt, lt
  Comparator #(.mode("unsigned"), .width(26)) comparator_3 (
    .a(AddressFromBus), .b(26'h3ffff88), .eq(comparator_3_eq));  // open: gt, lt
  Comparator #(.mode("unsigned"), .width(26)) comparator_4 (
    .a(AddressFromBus), .b(26'h3ffff8c), .eq(comparator_4_eq));  // open: gt, lt
  and and_1 (and_1_out, WriteEnable, comparator_1_eq);
  and and_2 (and_2_out, WriteEnable, comparator_2_eq);
  and and_3 (and_3_out, WriteEnable, comparator_3_eq);
  and and_4 (and_4_out, WriteEnable, comparator_4_eq);
  Clock clock_1 (.out(clock_1_out));
  Bit_Extender #(.in_width(32), .out_width(14), .\type ("zero")) bit_extender_1 (
    .in(DataFromBus), .out(bit_extender_1_out));
  Bit_Extender #(.in_width(32), .out_width(1), .\type ("zero")) bit_extender_2 (
    .in(DataFromBus), .out(bit_extender_2_out));
  Bit_Extender #(.in_width(32), .out_width(7), .\type ("zero")) bit_extender_3 (
    .in(DataFromBus), .out(bit_extender_3_out));
  Bit_Extender #(.in_width(32), .out_width(8), .\type ("zero")) bit_extender_4 (
    .in(DataFromBus), .out(bit_extender_4_out));
  Register #(.width(14)) Frequency (
    .D(bit_extender_1_out), .en(and_1_out), .clk(clock_1_out), .Q(BuzzerFrequency));  // open: clr
  Register #(.width(1)) Switch (
    .D(bit_extender_2_out), .en(and_2_out), .clk(clock_1_out), .Q(WriteEnableToBuzzer));  // open: clr
  Register #(.width(7)) Volume (
    .D(bit_extender_3_out), .en(and_3_out), .clk(clock_1_out), .Q(BuzzerVolume));  // open: clr
  Register DutyCycle (.D(bit_extender_4_out), .en(and_4_out), .clk(clock_1_out), .Q(BuzzerDutyCycle));  // open: clr
endmodule

module SliderController (
  input  [31:0] DataFromBus,
  input  [25:0] AddressFromBus,
  input  WriteEnableFromBus,
  input  [7:0] DataFromSlider,
  output WriteEnableToBus,
  output [31:0] DataToBus
);

  wire comparator_1_eq, not_1_out;

  not not_1 (not_1_out, WriteEnableFromBus);
  Comparator #(.mode("unsigned"), .width(26)) comparator_1 (
    .a(AddressFromBus), .b(26'h3ffff90), .eq(comparator_1_eq));  // open: gt, lt
  assign DataToBus = {{24{1'b0}}, DataFromSlider};  // Bit_Extender bit_extender_1
  and and_1 (WriteEnableToBus, comparator_1_eq, not_1_out);
endmodule
